# Fritzing sketch ADXL345SPI (saved by Fritzing 0.9.2b)
breadboards: 1

parts:
  Part1 = Arduino Uno (Rev3)
  J1 = rounded female pin header, 8 pins [form="♀ (female rounded)"]

nets:
  N1: Part1.D10_PWM/SS, J1.pin3
  N2: Part1.D11_PWM/MOSI, J1.pin7
  N3: Part1.D12/MISO, J1.pin6
  N4: Part1.D13/SCK, J1.pin8
  N5: Part1.GND, J1.pin1
  N6: Part1.3V3, J1.pin2

notes:
  GND
  VCC
  CS
  INT1
  INT2
  SDO
  SDA
  SCL
  Diagram shows pins of a typical ADXL345 breakout board such as GY-291, which has pullup resistors.

// code stored in the sketch: ADXL345I2C.ino
/*=====================================================================
  This program is free software: you can redistribute it and/or modify
  it under the terms of the GNU General Public License as published by
  the Free Software Foundation, either version 3 of the License, or
  (at your option) any later version.

  This program is distributed in the hope that it will be useful,
  but WITHOUT ANY WARRANTY; without even the implied warranty of
  MERCHANTABILITY or FITNESS FOR A PARTICULAR PURPOSE.  See the
  GNU General Public License for more details.

  You should have received a copy of the GNU General Public License
  along with this program.  If not, see <http://www.gnu.org/licenses/>.
  ---------------------------------------------------------------------
  Purpose : Interface to the ADXL345 accelerometer via I2C.
  Date    : 21 Nov 2015
  Boards  : ArduinoUno
  =====================================================================
*/

#include <Wire.h>

/* Normal or alternate I2C address of the module */
#define I2C_Add 0x1D //0x53

/* ADXL345 register addresses */
#define POWER_CTL 0x2D
#define DATA_FORMAT 0x31
#define X_Axis 0x32
#define Y_Axis 0x34
#define Z_Axis 0x36

/* Accelerometer range modes */
#define RANGE_2g 0
#define RANGE_4g 1
#define RANGE_8g 2
#define RANGE_16g 3

void setup()
{
  /* Initialise the I2C bus */
  Wire.begin(); 
 
  Serial.begin(9600);
 
  initADXL345(RANGE_2g);
}

void loop()
{
  Serial.print("X: ");
  Serial.print(readAxis(X_Axis));
 
  Serial.print(" Y: ");
  Serial.print(readAxis(Y_Axis));
 
  Serial.print(" Z: ");
  Serial.println(readAxis(Z_Axis));
  
  delay(100);
}

/* Read one of the 3 axis via the I2C interface */
int readAxis(byte axis)
{
  int data;
   
  Wire.beginTransmission(I2C_Add);
  Wire.write(axis);
  Wire.endTransmission();
 
  Wire.beginTransmission(I2C_Add);
  Wire.requestFrom(I2C_Add, 2);
 
  if (Wire.available()) {
    data = (int)Wire.read();
    data = data | (Wire.read() << 8);
  }
  else {
    data = 0;
  }
   
  Wire.endTransmission(); 

  return data;
}

/* Initialise the ADXL345 */
void initADXL345(byte range)
{
  Wire.beginTransmission(I2C_Add);
 
  /* Set the sensitivity of the module */
  Wire.write(DATA_FORMAT);
  Wire.write(range);
  Wire.endTransmission();
 
  /* Put the module into measurement mode to start taking measurements */
  Wire.beginTransmission(I2C_Add);
  Wire.write(POWER_CTL);
  Wire.write(0x08);
 
  Wire.endTransmission();
}

// code stored in the sketch: ADXL345SPI.ino
/*=====================================================================
  This program is free software: you can redistribute it and/or modify
  it under the terms of the GNU General Public License as published by
  the Free Software Foundation, either version 3 of the License, or
  (at your option) any later version.

  This program is distributed in the hope that it will be useful,
  but WITHOUT ANY WARRANTY; without even the implied warranty of
  MERCHANTABILITY or FITNESS FOR A PARTICULAR PURPOSE.  See the
  GNU General Public License for more details.

  You should have received a copy of the GNU General Public License
  along with this program.  If not, see <http://www.gnu.org/licenses/>.
  ---------------------------------------------------------------------
  Purpose : Interface to the ADXL345 accelerometer via SPI.
  Date    : 21 Nov 2015
  Boards  : ArduinoUno, LaunchPadF5529
  =====================================================================
*/

// Comment/uncomment as suitable for your hardware
// #define LaunchPadF5529

#ifdef LaunchPadF5529
int CS = P2_7;
#else
int CS = 10;
#endif


#include <SPI.h>

char POWER_CTL = 0x2D;
char DATA_FORMAT = 0x31;
char DATAX0 = 0x32;
char DATAX1 = 0x33;
char DATAY0 = 0x34;
char DATAY1 = 0x35;
char DATAZ0 = 0x36;
char DATAZ1 = 0x37;

char values[10];
int x,y,z;

void setup(){ 
  SPI.begin();
  SPI.setDataMode(SPI_MODE3);
  SPI.setBitOrder(MSBFIRST);

  Serial.begin(9600);
  
  pinMode(CS, OUTPUT);
  digitalWrite(CS, HIGH);
  
  writeRegister(DATA_FORMAT, 0x00); // -+2g
  writeRegister(POWER_CTL, 0x08);  //Measurement mode  
}

void loop(){
  // Reading 6 bytes of data starting at register DATAX0 will retrieve 
  // the x,y and z acceleration values from the ADXL345.
  readRegister(DATAX0, 6, values);

  // 10-bit acceleration values stored across 2 bytes.
  x = ((int)values[1]<<8)|(int)values[0];
  y = ((int)values[3]<<8)|(int)values[2];
  z = ((int)values[5]<<8)|(int)values[4];
  
  Serial.print(x, DEC);
  Serial.print(',');
  Serial.print(y, DEC);
  Serial.print(',');
  Serial.println(z, DEC);      
  delay(200); 
}

//This function will write a value to a register on the ADXL345.
//Parameters:
//  char registerAddress - The register to write a value to
//  char value - The value to be written to the specified register.
void writeRegister(char registerAddress, char value){
  digitalWrite(CS, LOW);
  SPI.transfer(registerAddress);
  SPI.transfer(value);
  digitalWrite(CS, HIGH);

  #ifndef LaunchPadF5529
  //delay(100); // may be required on Arduino Uno
  #endif
}

//This function will read a certain number of registers starting from a specified address and store their values in a buffer.
//Parameters:
//  char registerAddress - The register addresse to start the read sequence from.
//  int numBytes - The number of registers that should be read.
//  char * values - A pointer to a buffer where the results of the operation should be stored.
void readRegister(char registerAddress, int numBytes, char * values){
  //Since we're performing a read operation, the most significant bit of the register address should be set.
  char address = 0x80 | registerAddress;
  //If we're doing a multi-byte read, bit 6 needs to be set as well.
  if(numBytes > 1) address = address | 0x40;
  
  digitalWrite(CS, LOW);
  SPI.transfer(address);
  for(int i=0; i<numBytes; i++){
    values[i] = SPI.transfer(0x00);
  }
  digitalWrite(CS, HIGH);

  #ifndef LaunchPadF5529
  //delay(100); // may be required on Arduino Uno
  #endif
}
