# Fritzing sketch Blink-LaunchPadF5529 (saved by Fritzing 0.9.2b)
breadboards: 1

parts:
  J12 = male pin header, 9 pins [form="♂ (male)"]
  J13 = double row male pin header, 10 pins [form="♂ (male)"]  # not connected
  J14 = double row male pin header, 10 pins [form="♂ (male)"]  # not connected
  J15 = double row male pin header, 10 pins [form="♂ (male)"]
  J16 = double row male pin header, 10 pins [form="♂ (male)"]  # not connected
  J17 = male pin header, 9 pins [form="♂ (male)"]
  S5 = Pushbutton [package="[THT]"]  # not connected
  S6 = Pushbutton [package="[THT]"]  # not connected
  S7 = Pushbutton [package="[THT]"]  # not connected
  S8 = Pushbutton [package="[THT]"]  # not connected
  J18 = male pin header, 2 pins [form="♂ (male)"]  # not connected
  R2 = Resistor [tolerance=±5% resistance=100 package=THT]
  LED2 = LED - 5mm [color="Red (633nm)" package="5 mm [THT]"]
  J19 = male pin header, 3 pins [form="♂ (male)"]
  J20 = male pin header, 3 pins [form="♂ (male)"]  # not connected

nets:
  N1: J12.pin1, J17.pin1
  N2: J12.pin2, J17.pin2
  N3: J12.pin3, J17.pin3
  N4: J12.pin4, J17.pin4
  N5: J12.pin7, J17.pin7
  N6: J12.pin8, J17.pin8
  N7: J12.pin9, J17.pin9
  N8: J15.pin2, R2.Pin_0
  N9: R2.Pin_1, LED2.anode
  N10: LED2.cathode, J19.pin1

notes:
  GND
  CTS <<
  TST
  RST
  BSL
  RTS >>
  3V3
  5V
  RXD <<
  TXD >>
  P6.1
  USB
  P4.7
  P1.1
  P1.0
  P2.1
  P3.6
  P6.2
  P7.0
  P6.0
  P6.4
  P6.3
  P3.5
  P4.2
  P6.6
  P3.4
  P6.5
  P4.1
  P1.6
  P3.2
  P2.7
  P3.3
  P1.4
  P2.4
  P3.7
  P1.3
  P4.0
  P1.5
  P4.3
  P8.2
  P2.5
  P1.2
  P2.3
  IEDF
  MSP-EXP430F5529LP
  P8.1
  P2.6
  P3.0
  P3.1
  P2.2
  P7.4
  P2.0
  LED
  M430F5529
  Change code to blink LED via P2_0.

// code stored in the sketch: Blink.ino
/*=====================================================================
  This program is free software: you can redistribute it and/or modify
  it under the terms of the GNU General Public License as published by
  the Free Software Foundation, either version 3 of the License, or
  (at your option) any later version.

  This program is distributed in the hope that it will be useful,
  but WITHOUT ANY WARRANTY; without even the implied warranty of
  MERCHANTABILITY or FITNESS FOR A PARTICULAR PURPOSE.  See the
  GNU General Public License for more details.

  You should have received a copy of the GNU General Public License
  along with this program.  If not, see <http://www.gnu.org/licenses/>.
  ---------------------------------------------------------------------
  Purpose : Blink two LEDs alternatively.
  Date    : 21 Nov 2015
  Boards  : ArduinoUno, LaunchPadF5529
  =====================================================================
*/

// Comment/uncomment as suitable for your hardware
// #define LaunchPadF5529

#ifdef LaunchPadF5529
#define LED1 RED_LED // on-board, aka P1_0
#define LED2 GREEN_LED // on-board, aka P4_7
#else
#define LED1 13 // on-board
#define LED2 2 // external
#endif

void setup() {                
  pinMode(LED1, OUTPUT);
  pinMode(LED2, OUTPUT);
}

void loop() {
  digitalWrite(LED1, HIGH);
  digitalWrite(LED2, LOW);
  delay(1000);

  digitalWrite(LED1, LOW);
  digitalWrite(LED2, HIGH);
  delay(1000);
}

// code stored in the sketch: sss.ino
/*=====================================================================
  This program is free software: you can redistribute it and/or modify
  it under the terms of the GNU General Public License as published by
  the Free Software Foundation, either version 3 of the License, or
  (at your option) any later version.

  This program is distributed in the hope that it will be useful,
  but WITHOUT ANY WARRANTY; without even the implied warranty of
  MERCHANTABILITY or FITNESS FOR A PARTICULAR PURPOSE.  See the
  GNU General Public License for more details.

  You should have received a copy of the GNU General Public License
  along with this program.  If not, see <http://www.gnu.org/licenses/>.
  ---------------------------------------------------------------------
  Purpose : Blink two LEDs alternatively.
  Date    : 21 Nov 2015
  Board   : ArduinoUno, LaunchPadF5529
  =====================================================================
*/

// Comment/uncomment as suitable to your hardware
// #define LaunchPadF5529

#ifdef LaunchPadF5529
#define LED1 RED_LED // on-board, aka P1_0
#define LED2 GREEN_LED // on-board, aka P4_7
#else
#define LED1 13 // on-board
#define LED2 2 // external
#endif

void setup() {                
  pinMode(LED1, OUTPUT);
  pinMode(LED2, OUTPUT);
}

void loop() {
  digitalWrite(LED1, HIGH);
  digitalWrite(LED2, LOW);
  delay(1000);

  digitalWrite(LED1, LOW);
  digitalWrite(LED2, HIGH);
  delay(1000);
}
