# Fritzing sketch BuzzerPot-PWM (saved by Fritzing 0.9.2b)
breadboards: 1

parts:
  R4 = Resistor [tolerance=±5% resistance=100 package=THT]
  R5 = Rotary Potentiometer (Small) [maximum_resistance=10kΩ package=THT]
  J13 = Piezo Speaker
  J14 = male pin header, 9 pins [form="♂ (male)"]
  J15 = double row male pin header, 10 pins [form="♂ (male)"]  # not connected
  J16 = double row male pin header, 10 pins [form="♂ (male)"]
  J17 = double row male pin header, 10 pins [form="♂ (male)"]  # not connected
  J18 = double row male pin header, 10 pins [form="♂ (male)"]
  J19 = male pin header, 9 pins [form="♂ (male)"]
  S5 = Pushbutton [package="[THT]"]  # not connected
  S6 = Pushbutton [package="[THT]"]  # not connected
  S7 = Pushbutton [package="[THT]"]  # not connected
  S8 = Pushbutton [package="[THT]"]  # not connected
  J20 = male pin header, 2 pins [form="♂ (male)"]  # not connected
  R6 = Resistor [tolerance=±5% resistance=100 package=THT]  # not connected
  J21 = male pin header, 3 pins [form="♂ (male)"]
  J22 = male pin header, 3 pins [form="♂ (male)"]  # not connected

nets:
  N1: R4.Pin_0, J16.pin2
  N2: R4.Pin_1, J13.pin2
  N3: R5.leg2, J18.pin6
  N4: J13.pin1, J21.pin1
  N5: J14.pin1, J19.pin1
  N6: J14.pin2, J19.pin2
  N7: J14.pin3, J19.pin3
  N8: J14.pin4, J19.pin4
  N9: J14.pin7, J19.pin7
  N10: J14.pin8, J19.pin8
  N11: J14.pin9, J19.pin9

notes:
  LED
  GND
  P6.1
  µC samples the potentiometer value. It then uses PWM to drive the buzzer.
  CTS <<
  TST
  RST
  BSL
  RTS >>
  3V3
  5V
  RXD <<
  TXD >>
  USB
  P4.7
  P1.1
  P1.0
  P2.1
  P3.6
  P6.2
  P7.0
  P6.0
  P6.4
  P6.3
  P3.5
  P4.2
  P6.6
  P3.4
  P6.5
  P4.1
  P1.6
  P3.2
  P2.7
  P3.3
  P1.4
  P2.4
  P3.7
  P1.3
  P4.0
  P1.5
  P4.3
  P8.2
  P2.5
  P1.2
  P2.3
  IEDF
  MSP-EXP430F5529LP
  P8.1
  P2.6
  P3.0
  P3.1
  P2.2
  P7.4
  P2.0
  M430F5529

// code stored in the sketch: BuzzerPot.ino
/*=====================================================================
  This program is free software: you can redistribute it and/or modify
  it under the terms of the GNU General Public License as published by
  the Free Software Foundation, either version 3 of the License, or
  (at your option) any later version.

  This program is distributed in the hope that it will be useful,
  but WITHOUT ANY WARRANTY; without even the implied warranty of
  MERCHANTABILITY or FITNESS FOR A PARTICULAR PURPOSE.  See the
  GNU General Public License for more details.

  You should have received a copy of the GNU General Public License
  along with this program.  If not, see <http://www.gnu.org/licenses/>.
  ---------------------------------------------------------------------
  Purpose : Using a potentiometer, drive a buzzer. We illustrate two
            variations:
            DIRECT   : Buzzer is directly connected to potentiometer.
            WITH_PWM : Buzzer is sampled by microcontroller, which then
                       uses PWM to drive the buzzer.
  Date    : 21 Nov 2015
  Boards  : ArduinoUno, LaunchPadF5529
  =====================================================================
*/

// Comment/uncomment as suitable for your hardware
// #define LaunchPadF5529

#ifdef LaunchPadF5529
#define VREF 3300 // mV
#define AIN A3 // aka P6_3
#define ADC_MAX 4095
#define BUZZER_OUT P2_4
#else
#define VREF 1100 // mV
#define AIN A5 // aka 17
#define ADC_MAX 1023
#define BUZZER_OUT 3
#endif

// Variation: Drive buzzer via PWM: change the wiring first
//#define WITH_PWM

// Variation: Change the tone rather than loudness when WITH_PWM is defined
//#define VARY_TONE

void setup()
{
  Serial.begin(9600);

  #ifndef LaunchPadF5529
  // Since Uno has only a 10-bit ADC, improve accuracy using internal 1.1V
  analogReference(INTERNAL);
  #endif
}

void loop()
{
  int sensorValue = analogRead(AIN);
  int voltage = map(sensorValue,0,ADC_MAX,0,VREF); // for debugging

  #ifdef WITH_PWM
    #ifdef VARY_TONE
    int toneOut = map(sensorValue,0,ADC_MAX,100,10000);
    tone(BUZZER_OUT, toneOut);
    #else
    int writeOut = map(sensorValue,0,ADC_MAX,0,255);
    analogWrite(BUZZER_OUT, writeOut);
    #endif
  #endif

  Serial.print(sensorValue);
  Serial.print("\t");
  Serial.print(voltage);
  #ifdef WITH_PWM
    #ifdef VARY_TONE
    Serial.print("\t");
    Serial.println(toneOut);
    #else
    Serial.println(writeOut);
    #endif
  #else
    Serial.println("");
  #endif

  delay(50); // delay in between reads for stability
}
