# Fritzing sketch FC04-SoundSensor (saved by Fritzing 0.9.2b)
breadboards: 1

parts:
  Part1 = Arduino Uno (Rev3)
  LED7 = LED - 5mm [color="Red (633nm)" package="5 mm [THT]"]
  LED8 = LED - 5mm [color="Red (633nm)" package="5 mm [THT]"]
  LED9 = LED - 5mm [color="Red (633nm)" package="5 mm [THT]"]
  LED10 = LED - 5mm [color="Red (633nm)" package="5 mm [THT]"]
  LED11 = LED - 5mm [color="Red (633nm)" package="5 mm [THT]"]
  LED12 = LED - 5mm [color="Red (633nm)" package="5 mm [THT]"]
  R7 = Resistor [tolerance=±5% resistance=220 package=THT]
  R8 = Resistor [tolerance=±5% resistance=220 package=THT]
  R9 = Resistor [tolerance=±5% resistance=220 package=THT]
  R10 = Resistor [tolerance=±5% resistance=220 package=THT]
  R11 = Resistor [tolerance=±5% resistance=220 package=THT]
  R12 = Resistor [tolerance=±5% resistance=220 package=THT]
  J13 = female pin header, 3 pins [form="♀ (female)"]

nets:
  N1: Part1.A5/SCL, J13.pin1
  N2: Part1.D2, LED12.anode
  N3: Part1.D3_PWM, LED11.anode
  N4: Part1.D4, LED10.anode
  N5: Part1.D5_PWM, LED9.anode
  N6: Part1.D6_PWM, LED8.anode
  N7: Part1.D7, LED7.anode
  N8: Part1.3V3, J13.pin3
  N9: Part1.GND, R7.Pin_1, R8.Pin_1, R9.Pin_1, R10.Pin_1, R11.Pin_1, R12.Pin_1, J13.pin2
  N10: LED7.cathode, R7.Pin_0
  N11: LED8.cathode, R8.Pin_0
  N12: LED9.cathode, R9.Pin_0
  N13: LED10.cathode, R10.Pin_0
  N14: LED11.cathode, R11.Pin_0
  N15: LED12.cathode, R12.Pin_0

notes:
  GND
  OUT
  VCC
  FC04 Sensor
  Sensor analog value is read on A5. Six digital pins are used to drive the six LEDs. Supply to sensor is 3.3V. Resistors are all 220 ohms.

// code stored in the sketch: Blink.ino
/*=====================================================================
  This program is free software: you can redistribute it and/or modify
  it under the terms of the GNU General Public License as published by
  the Free Software Foundation, either version 3 of the License, or
  (at your option) any later version.

  This program is distributed in the hope that it will be useful,
  but WITHOUT ANY WARRANTY; without even the implied warranty of
  MERCHANTABILITY or FITNESS FOR A PARTICULAR PURPOSE.  See the
  GNU General Public License for more details.

  You should have received a copy of the GNU General Public License
  along with this program.  If not, see <http://www.gnu.org/licenses/>.
  ---------------------------------------------------------------------
  Purpose : Blink two LEDs alternatively. One LED is on the board and
            the other is connected externally.
  Date    : 21 Nov 2015
  Boards  : ArduinoUno, LaunchPadF5529
  =====================================================================
*/

// Comment/uncomment as suitable for your hardware
// #define LaunchPadF5529

#ifdef LaunchPadF5529
#define LED1 RED_LED // on-board, aka P1_0
#define LED2 GREEN_LED // on-board, aka P4_7
#else
#define LED1 13 // on-board
#define LED2 2 // external
#endif

void setup() {                
  pinMode(LED1, OUTPUT);
  pinMode(LED2, OUTPUT);
}

void loop() {
  digitalWrite(LED1, HIGH);
  digitalWrite(LED2, LOW);
  delay(1000);

  digitalWrite(LED1, LOW);
  digitalWrite(LED2, HIGH);
  delay(1000);
}

// code stored in the sketch: sss.ino
/*=====================================================================
  This program is free software: you can redistribute it and/or modify
  it under the terms of the GNU General Public License as published by
  the Free Software Foundation, either version 3 of the License, or
  (at your option) any later version.

  This program is distributed in the hope that it will be useful,
  but WITHOUT ANY WARRANTY; without even the implied warranty of
  MERCHANTABILITY or FITNESS FOR A PARTICULAR PURPOSE.  See the
  GNU General Public License for more details.

  You should have received a copy of the GNU General Public License
  along with this program.  If not, see <http://www.gnu.org/licenses/>.
  ---------------------------------------------------------------------
  Purpose : Blink two LEDs alternatively.
  Date    : 21 Nov 2015
  Board   : ArduinoUno, LaunchPadF5529
  =====================================================================
*/

// Comment/uncomment as suitable to your hardware
// #define LaunchPadF5529

#ifdef LaunchPadF5529
#define LED1 RED_LED // on-board, aka P1_0
#define LED2 GREEN_LED // on-board, aka P4_7
#else
#define LED1 13 // on-board
#define LED2 2 // external
#endif

void setup() {                
  pinMode(LED1, OUTPUT);
  pinMode(LED2, OUTPUT);
}

void loop() {
  digitalWrite(LED1, HIGH);
  digitalWrite(LED2, LOW);
  delay(1000);

  digitalWrite(LED1, LOW);
  digitalWrite(LED2, HIGH);
  delay(1000);
}
