# Fritzing sketch HC05-AT-Cmds-LaunchPadF5529 (saved by Fritzing 0.9.2b)
breadboards: 1

parts:
  S1 = Pushbutton [package="[THT]"]  # not connected
  S2 = Pushbutton [package="[THT]"]  # not connected
  S3 = Pushbutton [package="[THT]"]  # not connected
  S4 = Pushbutton [package="[THT]"]  # not connected
  J4 = male pin header, 2 pins [form="♂ (male)"]  # not connected
  J2 = double row male pin header, 10 pins [form="♂ (male)"]  # not connected
  J5 = double row male pin header, 10 pins [form="♂ (male)"]
  J6 = double row male pin header, 10 pins [form="♂ (male)"]  # not connected
  J7 = double row male pin header, 10 pins [form="♂ (male)"]
  J10 = male pin header, 3 pins [form="♂ (male)"]
  J11 = male pin header, 3 pins [form="♂ (male)"]
  J8 = male pin header, 9 pins [form="♂ (male)"]
  J9 = male pin header, 9 pins [form="♂ (male)"]
  J12 = female pin header, 6 pins [form="♀ (female)" part_number=ccc]

nets:
  N1: J5.pin2, J12.pin1
  N2: J7.pin3, J12.pin4
  N3: J7.pin4, J12.pin5
  N4: J10.pin3, J12.pin2
  N5: J11.pin1, J12.pin3
  N6: J8.pin1, J9.pin1
  N7: J8.pin2, J9.pin2
  N8: J8.pin3, J9.pin3
  N9: J8.pin4, J9.pin4
  N10: J8.pin7, J9.pin7
  N11: J8.pin8, J9.pin8
  N12: J8.pin9, J9.pin9

notes:
  GND
  LED
  P2.0
  P7.4
  P2.2
  RST
  P3.1
  P3.0
  P2.6
  P8.1
  P2.3
  P1.2
  P2.5
  P8.2
  P4.3
  P1.5
  P4.0
  P1.3
  P3.7
  P2.4
  P1.4
  P3.3
  P2.7
  P3.2
  P1.6
  P4.1
  P6.5
  P3.4
  P6.6
  3V3
  P4.2
  P3.5
  5V
  P6.3
  P6.4
  P6.0
  P7.0
  P6.2
  P3.6
  P6.1
  M430F5529
  RTS >>
  TXD >>
  RXD <<
  CTS <<
  TST
  BSL
  P2.1
  P1.1
  P1.0
  P4.7
  USB
  MSP-EXP430F5529LP
  IEDF
  HC05-BT-Module
  EN
  +5V
  TX
  RX
  STATE

// code stored in the sketch: HC05-AT-Cmds.ino
/*=====================================================================
  This program is free software: you can redistribute it and/or modify
  it under the terms of the GNU General Public License as published by
  the Free Software Foundation, either version 3 of the License, or
  (at your option) any later version.

  This program is distributed in the hope that it will be useful,
  but WITHOUT ANY WARRANTY; without even the implied warranty of
  MERCHANTABILITY or FITNESS FOR A PARTICULAR PURPOSE.  See the
  GNU General Public License for more details.

  You should have received a copy of the GNU General Public License
  along with this program.  If not, see <http://www.gnu.org/licenses/>.
  ---------------------------------------------------------------------
  Purpose : Put the Bluetooth module in AT command mode. Run a bunch of
            commands to configure the module. Module can be forced to
            enter AT command mode by long pressing the reset button
            before powering it up.
  Date    : 11 Mar 2016
  Boards  : ArduinoUno, LaunchPadF5529
  =====================================================================
*/

// Comment/uncomment as suitable for your hardware
// #define LaunchPadF5529

#ifdef LaunchPadF5529
#define EN_PIN P2_0
#else
#define EN_PIN 9
#define BT_TX 2
#define BT_RX 3
#endif

// SoftwareSerial is used so that the usual Serial can be
// used for debugging. SoftwareSerial does not support 25MHz
// platforms such as LaunchPadF5529.
// Comment/uncomment as suitable since #include within #ifdef is not compiling!
// For LaunchPadF5529
// #define Bluetooth Serial1 // P3_4 and P3_3
// For ArduinoUno
#include <SoftwareSerial.h>
SoftwareSerial Bluetooth(BT_TX, BT_RX);

void setup()
{
  Serial.begin(9600);
  
  pinMode(EN_PIN, OUTPUT);
  digitalWrite(EN_PIN, HIGH);

  // Default baud rate in AT command mode
  Bluetooth.begin(38400);

  Serial.print("Waiting for AT commands ... ");
}

void loop()
{
  if (Bluetooth.available())
    Serial.write(Bluetooth.read());

  if (Serial.available())
      Bluetooth.write(Serial.read());
}

// code stored in the sketch: HC05-Bluetooth.ino
/*=====================================================================
  This program is free software: you can redistribute it and/or modify
  it under the terms of the GNU General Public License as published by
  the Free Software Foundation, either version 3 of the License, or
  (at your option) any later version.

  This program is distributed in the hope that it will be useful,
  but WITHOUT ANY WARRANTY; without even the implied warranty of
  MERCHANTABILITY or FITNESS FOR A PARTICULAR PURPOSE.  See the
  GNU General Public License for more details.

  You should have received a copy of the GNU General Public License
  along with this program.  If not, see <http://www.gnu.org/licenses/>.
  ---------------------------------------------------------------------
  Purpose : Send commands from an Android device via Bluetooth to turn
            on/off or blink and LED. A suggested Android app is the
            Bluetooth SPP Tools Pro.
  Date    : 7 Jan 2016
  Boards  : ArduinoUno, LaunchPadF5529
  =====================================================================
*/

// Comment/uncomment as suitable for your hardware
// #define LaunchPadF5529

#ifdef LaunchPadF5529
#define LED RED_LED // on-board, aka P1_0
#else
#define LED 13 // on-board
#define BT_TX 2
#define BT_RX 3
#endif

// SoftwareSerial is used so that the usual Serial can be
// used for debugging. SoftwareSerial does not support 25MHz
// platforms such as LaunchPadF5529.
// Comment/uncomment as suitable since #include within #ifdef is not compiling!
// For LaunchPadF5529
// #define Bluetooth Serial1 // P3_4 and P3_3
// For ArduinoUno
#include <SoftwareSerial.h>
SoftwareSerial Bluetooth(BT_TX, BT_RX);

boolean ToBlink = false;

void setup()
{
  Serial.begin(9600);
  Serial.print("Starting... ");

  // Change this if your BT module is configured to a different rate
  // Or configured the BT module using AT commands
  Bluetooth.begin(38400);

  pinMode(LED, OUTPUT);

  Serial.println("done");
}

void loop()
{
  // Process commands received via BT
  if (Bluetooth.available()) {
    char dataFromBt = Bluetooth.read();
    Serial.print("Received from BT: 0x");
    Serial.println(dataFromBt, HEX);

    if (dataFromBt == '1') {
      Serial.println("Turning on...");
      digitalWrite(LED, HIGH);
      ToBlink = false;
    }
    else if (dataFromBt == '0') {
      Serial.println("Turning off...");
      digitalWrite(LED, LOW);
      ToBlink = false;
    }
    else if (dataFromBt == 'b') {
      Serial.println("Blinking...");
      ToBlink = true;
    }
  }

  // Send Serial commands to BT
  if (Serial.available()) {
    char buffer[64];
    int numBytes = Serial.readBytesUntil('\n', buffer, 63);
    buffer[numBytes] = 0;
    Bluetooth.println(buffer);
  }

  if (ToBlink) {
    digitalWrite(LED, HIGH);
    delay(250);
    digitalWrite(LED, LOW);
    delay(250);
  }
}

// code stored in the sketch: LM35.ino
/*=====================================================================
  This program is free software: you can redistribute it and/or modify
  it under the terms of the GNU General Public License as published by
  the Free Software Foundation, either version 3 of the License, or
  (at your option) any later version.

  This program is distributed in the hope that it will be useful,
  but WITHOUT ANY WARRANTY; without even the implied warranty of
  MERCHANTABILITY or FITNESS FOR A PARTICULAR PURPOSE.  See the
  GNU General Public License for more details.

  You should have received a copy of the GNU General Public License
  along with this program.  If not, see <http://www.gnu.org/licenses/>.
  ---------------------------------------------------------------------
  Purpose : Use analog input to read temperature measurement from LM35.
  Date    : 21 Nov 2015
  Boards  : ArduinoUno, LaunchPadF5529
  =====================================================================
*/

// Comment/uncomment as suitable for your hardware
 #define LaunchPadF5529

#ifdef LaunchPadF5529
#define VREF 3300 // mV
#define AIN A5 // aka P6_5
#define ADC_MAX 4095
#else
#define VREF 1100 // mV
#define AIN A5 // aka 19
#define ADC_MAX 1023
#endif

void setup()
{
  Serial.begin(9600);

  #ifndef LaunchPadF5529
  // Since Uno has only a 10-bit ADC, improve accuracy using internal 1.1V
  analogReference(INTERNAL);
  #endif
}

void loop()
{
  float temperature = (VREF*0.1*analogRead(AIN))/(ADC_MAX+1); // 10mV => 1 degree C
  Serial.print("Temperature is ");
  Serial.print(temperature, 1);
  Serial.println(" degree Celsius.");

  // Avoid float to reduce code size
  /*
  int temperature = map(analogRead(AIN),0,ADC_MAX,0,VREF); // 10mV => 1 degree C
  Serial.print("Temperature is ");
  Serial.print(temperature / 10);
  Serial.print(".");
  Serial.print(temperature % 10);
  Serial.println(" degree Celsius.");
  */
  
  delay(1000);
}
