# Fritzing sketch HC05-Bluetooth (saved by Fritzing 0.9.2b)
breadboards: 1

parts:
  Part1 = Arduino Uno (Rev3)
  J13 = female pin header, 6 pins [form="♀ (female)" part_number=ccc]

nets:
  N1: Part1.D2, J13.pin4
  N2: Part1.D3_PWM, J13.pin5
  N3: Part1.5V, J13.pin2
  N4: Part1.GND, J13.pin3

notes:
  HC05-BT-Module
  STATE
  RX
  TX
  GND
  +5V
  EN

// code stored in the sketch: Blink.ino
/*=====================================================================
  This program is free software: you can redistribute it and/or modify
  it under the terms of the GNU General Public License as published by
  the Free Software Foundation, either version 3 of the License, or
  (at your option) any later version.

  This program is distributed in the hope that it will be useful,
  but WITHOUT ANY WARRANTY; without even the implied warranty of
  MERCHANTABILITY or FITNESS FOR A PARTICULAR PURPOSE.  See the
  GNU General Public License for more details.

  You should have received a copy of the GNU General Public License
  along with this program.  If not, see <http://www.gnu.org/licenses/>.
  ---------------------------------------------------------------------
  Purpose : Blink two LEDs alternatively.
  Date    : 21 Nov 2015
  Boards  : ArduinoUno, LaunchPadF5529
  =====================================================================
*/

// Comment/uncomment as suitable for your hardware
// #define LaunchPadF5529

#ifdef LaunchPadF5529
#define LED1 RED_LED // on-board, aka P1_0
#define LED2 GREEN_LED // on-board, aka P4_7
#else
#define LED1 13 // on-board
#define LED2 2 // external
#endif

void setup() {                
  pinMode(LED1, OUTPUT);
  pinMode(LED2, OUTPUT);
}

void loop() {
  digitalWrite(LED1, HIGH);
  digitalWrite(LED2, LOW);
  delay(1000);

  digitalWrite(LED1, LOW);
  digitalWrite(LED2, HIGH);
  delay(1000);
}

// code stored in the sketch: HC05-AT-Cmds.ino
/*=====================================================================
  This program is free software: you can redistribute it and/or modify
  it under the terms of the GNU General Public License as published by
  the Free Software Foundation, either version 3 of the License, or
  (at your option) any later version.

  This program is distributed in the hope that it will be useful,
  but WITHOUT ANY WARRANTY; without even the implied warranty of
  MERCHANTABILITY or FITNESS FOR A PARTICULAR PURPOSE.  See the
  GNU General Public License for more details.

  You should have received a copy of the GNU General Public License
  along with this program.  If not, see <http://www.gnu.org/licenses/>.
  ---------------------------------------------------------------------
  Purpose : Put the Bluetooth module in AT command mode. Run a bunch of
            commands to configure the module. Module can be forced to
            enter AT command mode by long pressing the reset button
            before powering it up.
  Date    : 11 Mar 2016
  Boards  : ArduinoUno, LaunchPadF5529
  =====================================================================
*/

// Comment/uncomment as suitable for your hardware
// #define LaunchPadF5529

#ifdef LaunchPadF5529
#define EN_PIN P2_0
#else
#define BT_TX 2
#define BT_RX 3
#define EN_PIN 9
#endif

// SoftwareSerial is used so that the usual Serial can be
// used for debugging. SoftwareSerial does not support 25MHz
// platforms such as LaunchPadF5529.
// Comment/uncomment as suitable since #include within #ifdef is not compiling!
// For LaunchPadF5529
// #define Bluetooth Serial1 // P3_4 and P3_3
// For ArduinoUno
#include <SoftwareSerial.h>
SoftwareSerial Bluetooth(BT_TX, BT_RX);

void setup()
{
  Serial.begin(9600);
  
  pinMode(EN_PIN, OUTPUT);
  digitalWrite(EN_PIN, HIGH);

  // Default baud rate in AT command mode
  Bluetooth.begin(38400);

  Serial.print("Waiting for AT commands ... ");
}

void loop()
{
  if (Bluetooth.available())
    Serial.write(Bluetooth.read());

  if (Serial.available())
      Bluetooth.write(Serial.read());
}

// code stored in the sketch: HC05-Bluetooth.ino
/*=====================================================================
  This program is free software: you can redistribute it and/or modify
  it under the terms of the GNU General Public License as published by
  the Free Software Foundation, either version 3 of the License, or
  (at your option) any later version.

  This program is distributed in the hope that it will be useful,
  but WITHOUT ANY WARRANTY; without even the implied warranty of
  MERCHANTABILITY or FITNESS FOR A PARTICULAR PURPOSE.  See the
  GNU General Public License for more details.

  You should have received a copy of the GNU General Public License
  along with this program.  If not, see <http://www.gnu.org/licenses/>.
  ---------------------------------------------------------------------
  Purpose : Send commands from an Android device via Bluetooth to turn
            on/off or blink and LED. A suggested Android app is the
            Bluetooth SPP Tools Pro.
  Date    : 7 Jan 2016
  Boards  : ArduinoUno, LaunchPadF5529
  =====================================================================
*/

// Comment/uncomment as suitable for your hardware
// #define LaunchPadF5529

#ifdef LaunchPadF5529
#define LED RED_LED // on-board, aka P1_0
#else
#define LED 13 // on-board
#define BT_TX 2
#define BT_RX 3
#endif

// SoftwareSerial is used so that the usual Serial can be
// used for debugging. SoftwareSerial does not support 25MHz
// platforms such as LaunchPadF5529.
// Comment/uncomment as suitable since #include within #ifdef is not compiling!
// For LaunchPadF5529
// #define Bluetooth Serial1 // P3_4 and P3_3
// For ArduinoUno
#include <SoftwareSerial.h>
SoftwareSerial Bluetooth(BT_TX, BT_RX);

boolean ToBlink = false;

void setup()
{
  Serial.begin(9600);
  Serial.print("Starting... ");

  // Change this if your BT module is configured to a different rate
  // Or configure the BT module using AT commands
  Bluetooth.begin(9600);

  pinMode(LED, OUTPUT);

  Serial.println("done");
}

void loop()
{
  // Process commands received via BT
  if (Bluetooth.available()) {
    char dataFromBt = Bluetooth.read();
    Serial.print("Received from BT: 0x");
    Serial.println(dataFromBt, HEX);

    if (dataFromBt == '1') {
      Serial.println("Turning on...");
      digitalWrite(LED, HIGH);
      ToBlink = false;
    }
    else if (dataFromBt == '0') {
      Serial.println("Turning off...");
      digitalWrite(LED, LOW);
      ToBlink = false;
    }
    else if (dataFromBt == 'b') {
      Serial.println("Blinking...");
      ToBlink = true;
    }
  }

  // Send Serial commands to BT
  if (Serial.available()) {
    char buffer[64];
    int numBytes = Serial.readBytesUntil('\n', buffer, 63);
    buffer[numBytes] = 0;
    Bluetooth.println(buffer);
  }

  if (ToBlink) {
    digitalWrite(LED, HIGH);
    delay(250);
    digitalWrite(LED, LOW);
    delay(250);
  }
}

// code stored in the sketch: sss.ino
/*=====================================================================
  This program is free software: you can redistribute it and/or modify
  it under the terms of the GNU General Public License as published by
  the Free Software Foundation, either version 3 of the License, or
  (at your option) any later version.

  This program is distributed in the hope that it will be useful,
  but WITHOUT ANY WARRANTY; without even the implied warranty of
  MERCHANTABILITY or FITNESS FOR A PARTICULAR PURPOSE.  See the
  GNU General Public License for more details.

  You should have received a copy of the GNU General Public License
  along with this program.  If not, see <http://www.gnu.org/licenses/>.
  ---------------------------------------------------------------------
  Purpose : Blink two LEDs alternatively.
  Date    : 21 Nov 2015
  Board   : ArduinoUno, LaunchPadF5529
  =====================================================================
*/

// Comment/uncomment as suitable to your hardware
// #define LaunchPadF5529

#ifdef LaunchPadF5529
#define LED1 RED_LED // on-board, aka P1_0
#define LED2 GREEN_LED // on-board, aka P4_7
#else
#define LED1 13 // on-board
#define LED2 2 // external
#endif

void setup() {                
  pinMode(LED1, OUTPUT);
  pinMode(LED2, OUTPUT);
}

void loop() {
  digitalWrite(LED1, HIGH);
  digitalWrite(LED2, LOW);
  delay(1000);

  digitalWrite(LED1, LOW);
  digitalWrite(LED2, HIGH);
  delay(1000);
}
