# Fritzing sketch HCSR04-Ultrasonic (saved by Fritzing 0.9.2b)
breadboards: 1

parts:
  Part1 = Arduino Uno (Rev3)
  J1 = female pin header, 4 pins [form="♀ (female)"]

nets:
  N1: Part1.D2, J1.pin3
  N2: Part1.D3_PWM, J1.pin2

notes:
  VCC
  Trig
  GND
  Echo
  HCSR04 module is not shown. Only the header pins are shown below.

// code stored in the sketch: Blink.ino
/*=====================================================================
  This program is free software: you can redistribute it and/or modify
  it under the terms of the GNU General Public License as published by
  the Free Software Foundation, either version 3 of the License, or
  (at your option) any later version.

  This program is distributed in the hope that it will be useful,
  but WITHOUT ANY WARRANTY; without even the implied warranty of
  MERCHANTABILITY or FITNESS FOR A PARTICULAR PURPOSE.  See the
  GNU General Public License for more details.

  You should have received a copy of the GNU General Public License
  along with this program.  If not, see <http://www.gnu.org/licenses/>.
  ---------------------------------------------------------------------
  Purpose : Blink two LEDs alternatively.
  Date    : 21 Nov 2015
  Boards  : ArduinoUno, LaunchPadF5529
  =====================================================================
*/

// Comment/uncomment as suitable to your hardware
// #define LaunchPadF5529

#ifdef LaunchPadF5529
#define LED1 RED_LED // on-board, aka P1_0
#define LED2 GREEN_LED // on-board, aka P4_7
#else
#define LED1 13 // on-board
#define LED2 2 // external
#endif

void setup() {                
  pinMode(LED1, OUTPUT);
  pinMode(LED2, OUTPUT);
}

void loop() {
  digitalWrite(LED1, HIGH);
  digitalWrite(LED2, LOW);
  delay(1000);

  digitalWrite(LED1, LOW);
  digitalWrite(LED2, HIGH);
  delay(1000);
}

// code stored in the sketch: HCSR04-Ultrasonic.ino
/*=====================================================================
  This program is free software: you can redistribute it and/or modify
  it under the terms of the GNU General Public License as published by
  the Free Software Foundation, either version 3 of the License, or
  (at your option) any later version.

  This program is distributed in the hope that it will be useful,
  but WITHOUT ANY WARRANTY; without even the implied warranty of
  MERCHANTABILITY or FITNESS FOR A PARTICULAR PURPOSE.  See the
  GNU General Public License for more details.

  You should have received a copy of the GNU General Public License
  along with this program.  If not, see <http://www.gnu.org/licenses/>.
  ---------------------------------------------------------------------
  Purpose : Sense the distance of an object/obstacle using ultrasound.
  Date    : 21 Nov 2015
  Boards  : ArduinoUno, LaunchPadF5529
  =====================================================================
*/

// Comment/uncomment as suitable for your hardware
// #define LaunchPadF5529

#ifdef LaunchPadF5529
#define TriggerPin P2_0
#define EchoPin P2_2
#else
#define TriggerPin 2
#define EchoPin 3
#endif

#define VelocitySound 340 // meters/sec

void setup()
{
  Serial.begin(9600);
  pinMode(TriggerPin, OUTPUT);
  digitalWrite(TriggerPin, LOW);

  #ifdef LaunchPadF5529
  pinMode(EchoPin, INPUT_PULLDOWN);
  #else
  pinMode(EchoPin, INPUT);
  digitalWrite(EchoPin, HIGH);
  #endif
}

void loop()
{
  digitalWrite(TriggerPin, LOW);
  delayMicroseconds(2);
  digitalWrite(TriggerPin, HIGH);
  delayMicroseconds(10);
  digitalWrite(TriggerPin, LOW);

  unsigned int pulseDuration = pulseIn(EchoPin, HIGH);
  if (pulseDuration) {
    float distance = float(pulseDuration)*VelocitySound/20000; // us->s (/1000000); m->cm (*100)
    if (distance <= 2) { // minimum distance the sensor can measure
      Serial.println("Obstacle is too close.");
    }
    else if (distance > 400) { // maximum distance the sensor can measure
      Serial.println("Obstacle is probably out of range.");
    }
    else {
      Serial.print("Obstacle is ");
      Serial.print(distance);
      Serial.println(" cms away.");
    }
  }
  else {
    Serial.println("No obstacle detected.");
  }
  delay(500); // minimum measurement cycle recommended in 60ms
}

// code stored in the sketch: sss.ino
/*=====================================================================
  This program is free software: you can redistribute it and/or modify
  it under the terms of the GNU General Public License as published by
  the Free Software Foundation, either version 3 of the License, or
  (at your option) any later version.

  This program is distributed in the hope that it will be useful,
  but WITHOUT ANY WARRANTY; without even the implied warranty of
  MERCHANTABILITY or FITNESS FOR A PARTICULAR PURPOSE.  See the
  GNU General Public License for more details.

  You should have received a copy of the GNU General Public License
  along with this program.  If not, see <http://www.gnu.org/licenses/>.
  ---------------------------------------------------------------------
  Purpose : Blink two LEDs alternatively.
  Date    : 21 Nov 2015
  Board   : ArduinoUno, LaunchPadF5529
  =====================================================================
*/

// Comment/uncomment as suitable to your hardware
// #define LaunchPadF5529

#ifdef LaunchPadF5529
#define LED1 RED_LED // on-board, aka P1_0
#define LED2 GREEN_LED // on-board, aka P4_7
#else
#define LED1 13 // on-board
#define LED2 2 // external
#endif

void setup() {                
  pinMode(LED1, OUTPUT);
  pinMode(LED2, OUTPUT);
}

void loop() {
  digitalWrite(LED1, HIGH);
  digitalWrite(LED2, LOW);
  delay(1000);

  digitalWrite(LED1, LOW);
  digitalWrite(LED2, HIGH);
  delay(1000);
}
