# Fritzing sketch IR-Proximity-Detection (saved by Fritzing 0.9.2b)
breadboards: 1

parts:
  Part1 = Arduino Uno (Rev3)
  LED1 = LED - 5mm [color="Infrared (940nm)" package="5 mm [THT]"]
  R1 = Resistor [tolerance=±5% resistance=220 package=THT]
  R2 = Resistor [tolerance=±5% resistance=220 package=THT]
  LED2 = LED - 5mm [color="Red (635nm)" package="5 mm [THT]"]
  LED3 = LED - 5mm [color="Infrared (940nm)" package="5 mm [THT]"]
  R3 = Resistor [tolerance=±5% resistance=4.7k package=THT]

nets:
  N1: Part1.A5/SCL, LED3.cathode, R3.Pin_1
  N2: Part1.D5_PWM, R2.Pin_0
  N3: Part1.5V, R1.Pin_0, R3.Pin_0
  N4: Part1.GND, LED1.cathode, LED2.cathode, LED3.anode
  N5: LED1.anode, R1.Pin_1
  N6: R2.Pin_1, LED2.anode

notes:
  IR LED
  IR Photodiode
  Photodiodes are normally black in colour. They are reverse biased while IR LEDs are forward biased.

// code stored in the sketch: Blink.ino
/*=====================================================================
  This program is free software: you can redistribute it and/or modify
  it under the terms of the GNU General Public License as published by
  the Free Software Foundation, either version 3 of the License, or
  (at your option) any later version.

  This program is distributed in the hope that it will be useful,
  but WITHOUT ANY WARRANTY; without even the implied warranty of
  MERCHANTABILITY or FITNESS FOR A PARTICULAR PURPOSE.  See the
  GNU General Public License for more details.

  You should have received a copy of the GNU General Public License
  along with this program.  If not, see <http://www.gnu.org/licenses/>.
  ---------------------------------------------------------------------
  Purpose : Blink two LEDs alternatively. One LED is on the board and
            the other is connected externally.
  Date    : 21 Nov 2015
  Boards  : ArduinoUno, LaunchPadF5529
  =====================================================================
*/

// Comment/uncomment as suitable for your hardware
// #define LaunchPadF5529

#ifdef LaunchPadF5529
#define LED1 RED_LED // on-board, aka P1_0
#define LED2 GREEN_LED // on-board, aka P4_7
#else
#define LED1 13 // on-board
#define LED2 2 // external
#endif

void setup() {                
  pinMode(LED1, OUTPUT);
  pinMode(LED2, OUTPUT);
}

void loop() {
  digitalWrite(LED1, HIGH);
  digitalWrite(LED2, LOW);
  delay(1000);

  digitalWrite(LED1, LOW);
  digitalWrite(LED2, HIGH);
  delay(1000);
}

// code stored in the sketch: IR-Promixity-Detection.ino
/*=====================================================================
  This program is free software: you can redistribute it and/or modify
  it under the terms of the GNU General Public License as published by
  the Free Software Foundation, either version 3 of the License, or
  (at your option) any later version.

  This program is distributed in the hope that it will be useful,
  but WITHOUT ANY WARRANTY; without even the implied warranty of
  MERCHANTABILITY or FITNESS FOR A PARTICULAR PURPOSE.  See the
  GNU General Public License for more details.

  You should have received a copy of the GNU General Public License
  along with this program.  If not, see <http://www.gnu.org/licenses/>.
  ---------------------------------------------------------------------
  Purpose : Use an IR LED and an IR photodiode to detect proximity of
            an obstable. An indicator LED glows in response to the
            proximity of the obstable. This indicator can be programmed
            as a digital or an analog output.
  Date    : 16 Feb 2016
  Boards  : ArduinoUno, LaunchPadF5529
  =====================================================================
*/

// Comment/uncomment as suitable for your hardware
// #define LaunchPadF5529

#ifdef LaunchPadF5529
#define IRIN A5
#define LedIndicator P2_0
#else
#define IRIN A5
#define LedIndicator 5
#endif

// Default is an LED with varying brightness
// #define UseDigitalLed

unsigned int RefHighValue = 0;
unsigned int RefLowValue = 0;

unsigned int calibrate(unsigned int numSamples) {
  unsigned long sum = 0L;
  for (int i=0; i<numSamples; i++) {
    sum += analogRead(IRIN);
  }
  return sum/numSamples;  
}

void setup() {
  Serial.begin(9600);
  
  pinMode(LedIndicator, OUTPUT);
  #ifdef UseDigitalLed
  digitalWrite(LedIndicator, LOW);
  #else
  analogWrite(LedIndicator, 0);
  #endif

  RefHighValue = calibrate(100);
  Serial.print("Calibrated ADC high value (no obstacles): ");
  Serial.println(RefHighValue);

  Serial.println("Place obstacle and press enter to calibrate ...");
  while (!Serial.available()); // block till something is received
  while (Serial.available()) Serial.read(); // read all available bytes one by one
  RefLowValue = calibrate(100);
  Serial.print("Calibrated ADC low value (very close obstacle): ");
  Serial.println(RefLowValue);
}

void loop() {
  unsigned int readVal = analogRead(IRIN);
  int ledVal;
  
  #ifdef UseDigitalLed
  if (readVal < RefLowValue+(RefHighValue-RefLowValue)/2) ledVal = HIGH;
  else ledVal = LOW;
  digitalWrite(LedIndicator, ledVal);
  #else
  ledVal = map(readVal, RefLowValue, RefHighValue, 255, 0);
  if (ledVal<0) ledVal = 0;
  else if (ledVal>255) ledVal = 255;
  analogWrite(LedIndicator, ledVal);
  #endif

  // For debugging: comment out for more responsive behaviour
  Serial.print(readVal);
  Serial.print(" --> ");
  Serial.println(ledVal);

  delay(10);
}

// code stored in the sketch: sss.ino
/*=====================================================================
  This program is free software: you can redistribute it and/or modify
  it under the terms of the GNU General Public License as published by
  the Free Software Foundation, either version 3 of the License, or
  (at your option) any later version.

  This program is distributed in the hope that it will be useful,
  but WITHOUT ANY WARRANTY; without even the implied warranty of
  MERCHANTABILITY or FITNESS FOR A PARTICULAR PURPOSE.  See the
  GNU General Public License for more details.

  You should have received a copy of the GNU General Public License
  along with this program.  If not, see <http://www.gnu.org/licenses/>.
  ---------------------------------------------------------------------
  Purpose : Blink two LEDs alternatively.
  Date    : 21 Nov 2015
  Board   : ArduinoUno, LaunchPadF5529
  =====================================================================
*/

// Comment/uncomment as suitable to your hardware
// #define LaunchPadF5529

#ifdef LaunchPadF5529
#define LED1 RED_LED // on-board, aka P1_0
#define LED2 GREEN_LED // on-board, aka P4_7
#else
#define LED1 13 // on-board
#define LED2 2 // external
#endif

void setup() {                
  pinMode(LED1, OUTPUT);
  pinMode(LED2, OUTPUT);
}

void loop() {
  digitalWrite(LED1, HIGH);
  digitalWrite(LED2, LOW);
  delay(1000);

  digitalWrite(LED1, LOW);
  digitalWrite(LED2, HIGH);
  delay(1000);
}
