# Fritzing sketch LCD-2x16-Joystick (saved by Fritzing 0.9.2b)
breadboards: 1

parts:
  S1 = Pushbutton [package="[THT]"]  # not connected
  S2 = Pushbutton [package="[THT]"]  # not connected
  S3 = Pushbutton [package="[THT]"]  # not connected
  S4 = Pushbutton [package="[THT]"]  # not connected
  J4 = male pin header, 2 pins [form="♂ (male)"]  # not connected
  J2 = double row male pin header, 10 pins [form="♂ (male)"]
  J5 = double row male pin header, 10 pins [form="♂ (male)"]
  J6 = double row male pin header, 10 pins [form="♂ (male)"]
  J7 = double row male pin header, 10 pins [form="♂ (male)"]
  J10 = male pin header, 3 pins [form="♂ (male)"]  # not connected
  J11 = male pin header, 3 pins [form="♂ (male)"]  # not connected
  J8 = male pin header, 9 pins [form="♂ (male)"]
  J9 = male pin header, 9 pins [form="♂ (male)"]
  LCD1 = LCD screen
  R2 = Trimmer Potentiometer [maximum_resistance=10kΩ package=THT]
  R3 = Resistor [tolerance=±5% resistance=220 package=THT]
  U1 = JOYSTICK-PSP1000 [package=joystick-psp1000]

nets:
  N1: J2.pin1, LCD1.DB7
  N2: J2.pin2, LCD1.DB6
  N3: J2.pin3, LCD1.DB5
  N4: J2.pin4, LCD1.DB4
  N5: J5.pin1, LCD1.VSS, LCD1.R/W, LCD1.LED-, R2.leg2
  N6: J5.pin2, LCD1.RS
  N7: J5.pin3, LCD1.E
  N8: J6.pin1, LCD1.VDD, R2.leg1, R3.Pin_0
  N9: J6.pin2, U1.GND
  N10: J6.pin3, U1.X
  N11: J6.pin4, U1.Y
  N12: J7.pin1, U1.VCC
  N13: J8.pin1, J9.pin1
  N14: J8.pin2, J9.pin2
  N15: J8.pin3, J9.pin3
  N16: J8.pin4, J9.pin4
  N17: J8.pin7, J9.pin7
  N18: J8.pin8, J9.pin8
  N19: J8.pin9, J9.pin9
  N20: LCD1.V0, R2.wiper
  N21: LCD1.LED+, R3.Pin_1

notes:
  GND
  LED
  P2.0
  P7.4
  P2.2
  RST
  P3.1
  P3.0
  P2.6
  P8.1
  P2.3
  P1.2
  P2.5
  P8.2
  P4.3
  P1.5
  P4.0
  P1.3
  P3.7
  P2.4
  P1.4
  P3.3
  P2.7
  P3.2
  P1.6
  P4.1
  P6.5
  P3.4
  P6.6
  3V3
  P4.2
  P3.5
  5V
  P6.3
  P6.4
  P6.0
  P7.0
  P6.2
  P3.6
  P6.1
  M430F5529
  RTS >>
  TXD >>
  RXD <<
  CTS <<
  TST
  BSL
  P2.1
  P1.1
  P1.0
  P4.7
  USB
  MSP-EXP430F5529LP
  IEDF
  LCD is powered with 5V while joystick is at 3.3V. Data lines to the LCD are in yellow. Thus, 4-pin mode is used. Use trimmer to adjust LCD contrast.
  Joystick
  Y
  X

// code stored in the sketch: LCD-2x16-Joystick.ino
/*=====================================================================
  This program is free software: you can redistribute it and/or modify
  it under the terms of the GNU General Public License as published by
  the Free Software Foundation, either version 3 of the License, or
  (at your option) any later version.

  This program is distributed in the hope that it will be useful,
  but WITHOUT ANY WARRANTY; without even the implied warranty of
  MERCHANTABILITY or FITNESS FOR A PARTICULAR PURPOSE.  See the
  GNU General Public License for more details.

  You should have received a copy of the GNU General Public License
  along with this program.  If not, see <http://www.gnu.org/licenses/>.
  ---------------------------------------------------------------------
  Purpose : Read values from a joystick and display the same on a 2x16
            line LCD module. LiquidCrystal library is used in this
            example. 4-pin mode is used for the LCD. Since RW pin is
            grounded, only write operation is possible.
  Date    : 16 Dec 2015
  Boards  : ArduinoUno, LaunchPadF5529
  =====================================================================
*/

#include <LiquidCrystal.h>

// Comment/uncomment as suitable for your hardware
#define LaunchPadF5529

#ifdef LaunchPadF5529
#define VREF 3300 // mV
#define ADC_MAX 4095
LiquidCrystal lcd(P2_0, P2_2, P2_5, P2_4, P1_5, P1_4); // RS, E, D4, D5, D6, D7
#else
#define VREF 1100 // mV
#define ADC_MAX 1023
LiquidCrystal lcd(12, 11, 10, 5, 4, 3, 2); // RS, E, D4, D5, D6, D7
#endif

void setup()
{
  Serial.begin(9600);
  lcd.begin(16, 2);

  #ifndef LaunchPadF5529
  // Since Uno has only a 10-bit ADC, improve accuracy using internal 1.1V
  analogReference(INTERNAL);
  #endif
}

void loop()
{
  int xin = map(analogRead(A2), 0, ADC_MAX, 0, VREF);
  int yin = map(analogRead(A1), 0, ADC_MAX, 0, VREF);

  // For debugging
  Serial.print("Position (x, y): ");
  Serial.print(xin);
  Serial.print(", ");
  Serial.println(yin);
  
  lcd.clear(); // need to clear previous screen
  lcd.setCursor(0, 0);
  lcd.print("X: ");
  lcd.print(xin);
  lcd.setCursor(0, 1);
  lcd.print("Y: ");
  lcd.print(yin);

  delay(200);
}

// code stored in the sketch: LCD-2x16-Pot.ino
/*=====================================================================
  This program is free software: you can redistribute it and/or modify
  it under the terms of the GNU General Public License as published by
  the Free Software Foundation, either version 3 of the License, or
  (at your option) any later version.

  This program is distributed in the hope that it will be useful,
  but WITHOUT ANY WARRANTY; without even the implied warranty of
  MERCHANTABILITY or FITNESS FOR A PARTICULAR PURPOSE.  See the
  GNU General Public License for more details.

  You should have received a copy of the GNU General Public License
  along with this program.  If not, see <http://www.gnu.org/licenses/>.
  ---------------------------------------------------------------------
  Purpose : Use analog input to read temperature measurement from LM35.
  Date    : 21 Nov 2015
  Boards  : ArduinoUno, LaunchPadF5529
  =====================================================================
*/

// Comment/uncomment as suitable for your hardware
// #define LaunchPadF5529

#ifdef LaunchPadF5529
#define VREF 3300 // mV
#define AIN A5 // aka P6_5
#define ADC_MAX 4095
#else
#define VREF 1100 // mV
#define AIN A5 // aka 19
#define ADC_MAX 1023
#endif

void setup()
{
  Serial.begin(9600);

  #ifndef LaunchPadF5529
  // Since Uno has only a 10-bit ADC, improve accuracy using internal 1.1V
  analogReference(INTERNAL);
  #endif
}

void loop()
{
  float temperature = (VREF*0.1*analogRead(AIN))/(ADC_MAX+1); // 10mV => 1 degree C
  Serial.print("Temperature is ");
  Serial.print(temperature, 1);
  Serial.println(" degree Celsius.");

  // Avoid float to reduce code size
  /*
  int temperature = map(analogRead(AIN),0,ADC_MAX,0,VREF); // 10mV => 1 degree C
  Serial.print("Temperature is ");
  Serial.print(temperature / 10);
  Serial.print(".");
  Serial.print(temperature % 10);
  Serial.println(" degree Celsius.");
  */
  
  delay(1000);
}

// code stored in the sketch: LM35.ino
/*=====================================================================
  This program is free software: you can redistribute it and/or modify
  it under the terms of the GNU General Public License as published by
  the Free Software Foundation, either version 3 of the License, or
  (at your option) any later version.

  This program is distributed in the hope that it will be useful,
  but WITHOUT ANY WARRANTY; without even the implied warranty of
  MERCHANTABILITY or FITNESS FOR A PARTICULAR PURPOSE.  See the
  GNU General Public License for more details.

  You should have received a copy of the GNU General Public License
  along with this program.  If not, see <http://www.gnu.org/licenses/>.
  ---------------------------------------------------------------------
  Purpose : Use analog input to read temperature measurement from LM35.
  Date    : 21 Nov 2015
  Boards  : ArduinoUno, LaunchPadF5529
  =====================================================================
*/

// Comment/uncomment as suitable for your hardware
// #define LaunchPadF5529

#ifdef LaunchPadF5529
#define VREF 3300 // mV
#define AIN A5 // aka P6_5
#define ADC_MAX 4095
#else
#define VREF 1100 // mV
#define AIN A5 // aka 19
#define ADC_MAX 1023
#endif

void setup()
{
  Serial.begin(9600);

  #ifndef LaunchPadF5529
  // Since Uno has only a 10-bit ADC, improve accuracy using internal 1.1V
  analogReference(INTERNAL);
  #endif
}

void loop()
{
  float temperature = (VREF*0.1*analogRead(AIN))/(ADC_MAX+1); // 10mV => 1 degree C
  Serial.print("Temperature is ");
  Serial.print(temperature, 1);
  Serial.println(" degree Celsius.");

  // Avoid float to reduce code size
  /*
  int temperature = map(analogRead(AIN),0,ADC_MAX,0,VREF); // 10mV => 1 degree C
  Serial.print("Temperature is ");
  Serial.print(temperature / 10);
  Serial.print(".");
  Serial.print(temperature % 10);
  Serial.println(" degree Celsius.");
  */
  
  delay(1000);
}
