# Fritzing sketch LDR-LaunchPadF5529 (saved by Fritzing 0.9.2b)
breadboards: 1

parts:
  S1 = Pushbutton [package="[THT]"]  # not connected
  S2 = Pushbutton [package="[THT]"]  # not connected
  S3 = Pushbutton [package="[THT]"]  # not connected
  S4 = Pushbutton [package="[THT]"]  # not connected
  J4 = male pin header, 2 pins [form="♂ (male)"]  # not connected
  J2 = double row male pin header, 10 pins [form="♂ (male)"]  # not connected
  J5 = double row male pin header, 10 pins [form="♂ (male)"]  # not connected
  J6 = double row male pin header, 10 pins [form="♂ (male)"]  # not connected
  J7 = double row male pin header, 10 pins [form="♂ (male)"]
  J10 = male pin header, 3 pins [form="♂ (male)"]  # not connected
  J11 = male pin header, 3 pins [form="♂ (male)"]
  J8 = male pin header, 9 pins [form="♂ (male)"]
  J9 = male pin header, 9 pins [form="♂ (male)"]
  R2 = Photocell (LDR) [package=THT]
  R3 = Resistor [tolerance=±5% resistance=15k package=THT]  # not connected

nets:
  N1: J7.pin2, R2.pin_0
  N2: J11.pin1, R2.pin_1
  N3: J8.pin1, J9.pin1
  N4: J8.pin2, J9.pin2
  N5: J8.pin3, J9.pin3
  N6: J8.pin4, J9.pin4
  N7: J8.pin7, J9.pin7
  N8: J8.pin8, J9.pin8
  N9: J8.pin9, J9.pin9

notes:
  GND
  LED
  P2.0
  P7.4
  P2.2
  RST
  P3.1
  P3.0
  P2.6
  P8.1
  P2.3
  P1.2
  P2.5
  P8.2
  P4.3
  P1.5
  P4.0
  P1.3
  P3.7
  P2.4
  P1.4
  P3.3
  P2.7
  P3.2
  P1.6
  P4.1
  P6.5
  P3.4
  P6.6
  3V3
  P4.2
  P3.5
  5V
  P6.3
  P6.4
  P6.0
  P7.0
  P6.2
  P3.6
  P6.1
  M430F5529
  RTS >>
  TXD >>
  RXD <<
  CTS <<
  TST
  BSL
  P2.1
  P1.1
  P1.0
  P4.7
  USB
  MSP-EXP430F5529LP
  IEDF
  Update code if you use a different resistor value.

// code stored in the sketch: LDR.ino
/*=====================================================================
  This program is free software: you can redistribute it and/or modify
  it under the terms of the GNU General Public License as published by
  the Free Software Foundation, either version 3 of the License, or
  (at your option) any later version.

  This program is distributed in the hope that it will be useful,
  but WITHOUT ANY WARRANTY; without even the implied warranty of
  MERCHANTABILITY or FITNESS FOR A PARTICULAR PURPOSE.  See the
  GNU General Public License for more details.

  You should have received a copy of the GNU General Public License
  along with this program.  If not, see <http://www.gnu.org/licenses/>.
  ---------------------------------------------------------------------
  Purpose : LDR is a light dependant resistor. Read the analog voltage
            across the LDR and derive the resistance.
  Date    : 21 Nov 2015
  Boards  : ArduinoUno, LaunchPadF5529
  =====================================================================
*/

// Comment/uncomment as suitable for your hardware
// #define LaunchPadF5529

#ifdef LaunchPadF5529
#define AIN A5 // aka P6_5
#define ADC_MAX 4095
#else
#define AIN A5 // aka 19
#define ADC_MAX 1023
#endif

#define R1 10 // in kilo-ohms
#define Vcc 3300 // in mV

void setup()
{
  Serial.begin(9600);
}

void loop()
{
  int value = analogRead(AIN);
  unsigned int voltage = map(value, 0, ADC_MAX, 0, 3300);
  unsigned int resistance = voltage*R1/(Vcc-voltage); // comes from voltage divider concept
  
  Serial.print("Value: ");
  Serial.print(value);
  Serial.print("; Voltage (mV): ");
  Serial.print(voltage);
  Serial.print(" of ");
  Serial.print(Vcc);
  Serial.print("; Resistance (kilo-ohms): ");
  Serial.println(resistance);

  delay(1000);
}
