# Fritzing sketch LM35-7Segx3-LaunchPadF5529 (saved by Fritzing 0.9.3b)
breadboards: 1

parts:
  S1 = Pushbutton [package="[THT]"]  # not connected
  S2 = Pushbutton [package="[THT]"]  # not connected
  S3 = Pushbutton [package="[THT]"]  # not connected
  S4 = Pushbutton [package="[THT]"]  # not connected
  J4 = male pin header, 2 pins [form="♂ (male)"]  # not connected
  J2 = double row male pin header, 10 pins [form="♂ (male)"]  # not connected
  J5 = double row male pin header, 10 pins [form="♂ (male)"]
  J6 = double row male pin header, 10 pins [form="♂ (male)"]  # not connected
  J7 = double row male pin header, 10 pins [form="♂ (male)"]
  J10 = male pin header, 3 pins [form="♂ (male)"]
  J11 = male pin header, 3 pins [form="♂ (male)"]
  J8 = male pin header, 9 pins [form="♂ (male)"]
  J9 = male pin header, 9 pins [form="♂ (male)"]
  T1 = LM35 Temperature Sensor [package="TO92 [THT]"]
  7_Segment1 = 7 Segment Display  # not connected
  7_Segment2 = 7 Segment Display  # not connected
  7_Segment3 = 7 Segment Display  # not connected
  U1 = 74HC595 [package="DIP16 [THT]"]  # not connected
  R1 = Resistor [tolerance=±5% resistance=100 package=THT]
  R2 = Resistor [tolerance=±5% resistance=100 package=THT]
  R3 = Resistor [tolerance=±5% resistance=100 package=THT]

nets:
  N1: J5.pin2, R3.Pin_1
  N2: J5.pin3, R2.Pin_1
  N3: J5.pin4, R1.Pin_1
  N4: J7.pin2, T1.Vout
  N5: J10.pin3, T1.+Vs
  N6: J11.pin1, T1.GND
  N7: J8.pin1, J9.pin1
  N8: J8.pin2, J9.pin2
  N9: J8.pin3, J9.pin3
  N10: J8.pin4, J9.pin4
  N11: J8.pin7, J9.pin7
  N12: J8.pin8, J9.pin8
  N13: J8.pin9, J9.pin9

notes:
  GND
  LED
  P2.0
  P7.4
  P2.2
  RST
  P3.1
  P3.0
  P2.6
  P8.1
  P2.3
  P1.2
  P2.5
  P8.2
  P4.3
  P1.5
  P4.0
  P1.3
  P3.7
  P2.4
  P1.4
  P3.3
  P2.7
  P3.2
  P1.6
  P4.1
  P6.5
  P3.4
  P6.6
  3V3
  P4.2
  P3.5
  5V
  P6.3
  P6.4
  P6.0
  P7.0
  P6.2
  P3.6
  P6.1
  M430F5529
  RTS >>
  TXD >>
  RXD <<
  CTS <<
  TST
  BSL
  P2.1
  P1.1
  P1.0
  P4.7
  USB
  MSP-EXP430F5529LP
  Common cathode displays. Digits enabled via grey wires. Configuration hgfedcba. RCLK: P1.2, SCLK: P1.3, DATA: P2.5. Temperature read on P6.5.

// code stored in the sketch: LM35-7Segx3.ino
/*=====================================================================
  This program is free software: you can redistribute it and/or modify
  it under the terms of the GNU General Public License as published by
  the Free Software Foundation, either version 3 of the License, or
  (at your option) any later version.

  This program is distributed in the hope that it will be useful,
  but WITHOUT ANY WARRANTY; without even the implied warranty of
  MERCHANTABILITY or FITNESS FOR A PARTICULAR PURPOSE.  See the
  GNU General Public License for more details.

  You should have received a copy of the GNU General Public License
  along with this program.  If not, see <http://www.gnu.org/licenses/>.
  ---------------------------------------------------------------------
  Purpose : Use LM35 to sense temperature that is displayed. 
            Use 74HC595 shift register to control 3 7-segment displays.
  Date    : 21 Nov 2015
  Boards  : ArduinoUno, LaunchPadF5529
  =====================================================================
*/

// Comment/uncomment as suitable for your hardware
// #define LaunchPadF5529

#ifdef LaunchPadF5529
#define VREF 3300 // mV
#define AIN A5 // aka P6_5
#define ADC_MAX 4095
const int SCLK = P1_3, RCLK = P1_2, DATA = P2_5;
const int DIGIT1 = P2_0, DIGIT2 = P2_2, DIGIT3 = P7_4;
#else
#define VREF 1100 // mV
#define AIN A5 // aka 19
#define ADC_MAX 1023
const int SCLK = 2, RCLK = 3, DATA = 4;
const int DIGIT1 = 5, DIGIT2 = 6, DIGIT3 = 7;
#endif

// Ref. http://en.wikipedia.org/wiki/Seven-segment_display
char ledCodes[] = {
  0x3F, 0x06, 0x5B, 0x4F, 0x66, 0x6D, 0x7D, 0x07, 0x7F, 0x6F // gfedcba configuration: 0-9
};

void clockPulse()
{
  digitalWrite(SCLK, HIGH);
  digitalWrite(SCLK, LOW);
  digitalWrite(RCLK, HIGH);
  digitalWrite(RCLK, LOW);
}

void setShiftRegister8bit(int code)
{
   for (int i = 0; i < 8; i++)
   {
     digitalWrite(DATA, (((1 << i) & code) != 0) ? HIGH : LOW);
     clockPulse(); 
   }
}

void flashDigit(int signalOutput, int delayTime = 1)
{
  digitalWrite(signalOutput, LOW);
  delay(delayTime);
  digitalWrite(signalOutput, HIGH); 
}

void showDigit(int digitValue, int dot, int digitIndex)
{
    setShiftRegister8bit(ledCodes[digitValue] | dot<<7);
    flashDigit(digitIndex, 5);
}

void setup()
{
  #ifndef LaunchPadF5529
  // Since Uno has only a 10-bit ADC, improve accuracy using internal 1.1V
  analogReference(INTERNAL);
  #endif
  
  Serial.begin(9600); 
  
  pinMode(SCLK, OUTPUT);
  pinMode(RCLK, OUTPUT);
  pinMode(DATA, OUTPUT);
  pinMode(DIGIT1, OUTPUT);
  pinMode(DIGIT2, OUTPUT);
  pinMode(DIGIT3, OUTPUT);

  digitalWrite(DATA, LOW);
  digitalWrite(DIGIT1, HIGH);
  digitalWrite(DIGIT2, HIGH);
  digitalWrite(DIGIT3, HIGH);
  
  // Flash all segments of all digits
  setShiftRegister8bit(0xFF);
  digitalWrite(DIGIT1, LOW);
  digitalWrite(DIGIT2, LOW); 
  digitalWrite(DIGIT3, LOW);  
  delay(1000);
  digitalWrite(DIGIT1, HIGH);
  digitalWrite(DIGIT2, HIGH);  
  digitalWrite(DIGIT3, HIGH);  
  
  // Flash each segment of each digit one at a time
  for (int i = 0; i < 8; i++)
  {
    setShiftRegister8bit(1<<i);
    flashDigit(DIGIT1, 100);
    flashDigit(DIGIT2, 100);
    flashDigit(DIGIT3, 100);
    delay(100);
  }
}

int currTs = 0, lastTs = 0;
int lastReading = 0, part = 0;

void loop()
{
  currTs = millis();
  if (currTs - lastTs > 1000) { // Read sensor value once per second
    lastReading = map(analogRead(AIN),0,ADC_MAX,0,VREF); // 10mV => 1 degree C
    lastTs = currTs;
    Serial.println(lastReading); // for debugging
  }

  // All three digits are controlled by a single shift register.
  // Therefore, we cannot have any delay in the loop for flicker-free display.
  // To human vision, it will appear as though all three digits are
  // controlled at the same time. In reality, they are driven one by one.
  showDigit(lastReading / 100, 0, DIGIT1);
  part = lastReading % 100;
  showDigit(part / 10, 1, DIGIT2);
  showDigit(part % 10, 0, DIGIT3);
}
