# Fritzing sketch LM35-7Segx3 (saved by Fritzing 0.9.3b)
breadboards: 1

parts:
  Part1 = Arduino Uno (Rev3)
  T2 = LM35 Temperature Sensor [package="TO92 [THT]"]
  7_Segment4 = 7 Segment Display
  7_Segment5 = 7 Segment Display
  7_Segment6 = 7 Segment Display
  U2 = 74HC595 [package="DIP16 [THT]"]
  R1 = Resistor [tolerance=±5% resistance=220 package=THT]
  R2 = Resistor [tolerance=±5% resistance=220 package=THT]
  R3 = Resistor [tolerance=±5% resistance=220 package=THT]

nets:
  N1: Part1.A5/SCL, T2.Vout
  GND: Part1.GND, T2.GND, U2.GND, U2.OE
  N2: Part1.D2, U2.SH_CP
  N3: Part1.D3_PWM, U2.ST_CP
  N4: Part1.D4, U2.DS
  N5: Part1.D5_PWM, R1.Pin_0
  N6: Part1.D6_PWM, R2.Pin_0
  N7: Part1.D7, R3.Pin_0
  3V3: Part1.3V3, U2.MR, U2.VCC
  N8: Part1.5V, T2.+Vs
  N9: 7_Segment4.Segment_E, 7_Segment5.Segment_E, 7_Segment6.Segment_E, U2.Q3
  N10: 7_Segment4.Segment_D, 7_Segment5.Segment_D, 7_Segment6.Segment_D, U2.Q4
  N11: 7_Segment4.common_anode, R2.Pin_1
  N12: 7_Segment4.Segment_C, 7_Segment5.Segment_C, 7_Segment6.Segment_C, U2.Q5
  N13: 7_Segment4.Segment_DP, 7_Segment5.Segment_DP, 7_Segment6.Segment_DP, U2.Q0
  N14: 7_Segment4.Segment_B, 7_Segment5.Segment_B, 7_Segment6.Segment_B, U2.Q6
  N15: 7_Segment4.Segment_A, 7_Segment5.Segment_A, 7_Segment6.Segment_A, U2.Q7
  N16: 7_Segment4.Segment_F, 7_Segment5.Segment_F, 7_Segment6.Segment_F, U2.Q2
  N17: 7_Segment4.Segment_G, 7_Segment5.Segment_G, 7_Segment6.Segment_G, U2.Q1
  N18: 7_Segment5.common_anode, R3.Pin_1
  N19: 7_Segment6.common_anode, R1.Pin_1

notes:
  Common cathode displays. Digits enabled via grey wires. Configuration hgfedcba. SCLK: 2, RCLK: 3, DATA: 4. Temperature read on A5.

// code stored in the sketch: Blink.ino
/*=====================================================================
  This program is free software: you can redistribute it and/or modify
  it under the terms of the GNU General Public License as published by
  the Free Software Foundation, either version 3 of the License, or
  (at your option) any later version.

  This program is distributed in the hope that it will be useful,
  but WITHOUT ANY WARRANTY; without even the implied warranty of
  MERCHANTABILITY or FITNESS FOR A PARTICULAR PURPOSE.  See the
  GNU General Public License for more details.

  You should have received a copy of the GNU General Public License
  along with this program.  If not, see <http://www.gnu.org/licenses/>.
  ---------------------------------------------------------------------
  Purpose : Blink two LEDs alternatively.
  Date    : 21 Nov 2015
  Boards  : ArduinoUno, LaunchPadF5529
  =====================================================================
*/

// Comment/uncomment as suitable to your hardware
// #define LaunchPadF5529

#ifdef LaunchPadF5529
#define LED1 RED_LED // on-board, aka P1_0
#define LED2 GREEN_LED // on-board, aka P4_7
#else
#define LED1 13 // on-board
#define LED2 2 // external
#endif

void setup() {                
  pinMode(LED1, OUTPUT);
  pinMode(LED2, OUTPUT);
}

void loop() {
  digitalWrite(LED1, HIGH);
  digitalWrite(LED2, LOW);
  delay(1000);

  digitalWrite(LED1, LOW);
  digitalWrite(LED2, HIGH);
  delay(1000);
}

// code stored in the sketch: HCSR04-Ultrasonic.ino
/*=====================================================================
  This program is free software: you can redistribute it and/or modify
  it under the terms of the GNU General Public License as published by
  the Free Software Foundation, either version 3 of the License, or
  (at your option) any later version.

  This program is distributed in the hope that it will be useful,
  but WITHOUT ANY WARRANTY; without even the implied warranty of
  MERCHANTABILITY or FITNESS FOR A PARTICULAR PURPOSE.  See the
  GNU General Public License for more details.

  You should have received a copy of the GNU General Public License
  along with this program.  If not, see <http://www.gnu.org/licenses/>.
  ---------------------------------------------------------------------
  Purpose : Sense the distance of an object/obstacle using ultrasound.
  Date    : 21 Nov 2015
  Boards  : ArduinoUno, LaunchPadF5529
  =====================================================================
*/

// Comment/uncomment as suitable for your hardware
// #define LaunchPadF5529

#ifdef LaunchPadF5529
#define TriggerPin P2_0
#define EchoPin P2_2
#else
#define TriggerPin 2
#define EchoPin 3
#endif

#define VelocitySound 340 // meters/sec

void setup()
{
  Serial.begin(9600);
  pinMode(TriggerPin, OUTPUT);
  digitalWrite(TriggerPin, LOW);

  #ifdef LaunchPadF5529
  pinMode(EchoPin, INPUT_PULLDOWN);
  #else
  pinMode(EchoPin, INPUT);
  digitalWrite(EchoPin, HIGH);
  #endif
}

void loop()
{
  digitalWrite(TriggerPin, LOW);
  delayMicroseconds(2);
  digitalWrite(TriggerPin, HIGH);
  delayMicroseconds(10);
  digitalWrite(TriggerPin, LOW);

  unsigned int pulseDuration = pulseIn(EchoPin, HIGH);
  if (pulseDuration) {
    float distance = float(pulseDuration)*VelocitySound/20000; // us->s (/1000000); m->cm (*100)
    if (distance <= 2) { // minimum distance the sensor can measure
      Serial.println("Obstacle is too close.");
    }
    else if (distance > 400) { // maximum distance the sensor can measure
      Serial.println("Obstacle is probably out of range.");
    }
    else {
      Serial.print("Obstacle is ");
      Serial.print(distance);
      Serial.println(" cms away.");
    }
  }
  else {
    Serial.println("No obstacle detected.");
  }
  delay(500); // minimum measurement cycle recommended in 60ms
}

// code stored in the sketch: sss.ino
/*=====================================================================
  This program is free software: you can redistribute it and/or modify
  it under the terms of the GNU General Public License as published by
  the Free Software Foundation, either version 3 of the License, or
  (at your option) any later version.

  This program is distributed in the hope that it will be useful,
  but WITHOUT ANY WARRANTY; without even the implied warranty of
  MERCHANTABILITY or FITNESS FOR A PARTICULAR PURPOSE.  See the
  GNU General Public License for more details.

  You should have received a copy of the GNU General Public License
  along with this program.  If not, see <http://www.gnu.org/licenses/>.
  ---------------------------------------------------------------------
  Purpose : Blink two LEDs alternatively.
  Date    : 21 Nov 2015
  Board   : ArduinoUno, LaunchPadF5529
  =====================================================================
*/

// Comment/uncomment as suitable to your hardware
// #define LaunchPadF5529

#ifdef LaunchPadF5529
#define LED1 RED_LED // on-board, aka P1_0
#define LED2 GREEN_LED // on-board, aka P4_7
#else
#define LED1 13 // on-board
#define LED2 2 // external
#endif

void setup() {                
  pinMode(LED1, OUTPUT);
  pinMode(LED2, OUTPUT);
}

void loop() {
  digitalWrite(LED1, HIGH);
  digitalWrite(LED2, LOW);
  delay(1000);

  digitalWrite(LED1, LOW);
  digitalWrite(LED2, HIGH);
  delay(1000);
}
