# Fritzing sketch LedMatrix (saved by Fritzing 0.9.2b)

parts:
  Part1 = Arduino Uno (Rev3)
  R1 = Resistor [tolerance=±5% resistance=330 package=THT]
  R2 = Resistor [tolerance=±5% resistance=330 package=THT]
  R3 = Resistor [tolerance=±5% resistance=330 package=THT]
  R4 = Resistor [tolerance=±5% resistance=330 package=THT]
  R5 = Resistor [tolerance=±5% resistance=330 package=THT]
  R6 = Resistor [tolerance=±5% resistance=330 package=THT]
  R7 = Resistor [tolerance=±5% resistance=330 package=THT]
  R8 = Resistor [tolerance=±5% resistance=330 package=THT]
  Part2 = LED Matrix - Serial Interface - Red/Green/Blue
  J2 = female pin header, 2 pins [form="♀ (female)"]
  J3 = female pin header, 2 pins [form="♀ (female)"]

nets:
  N1: Part1.A1, R3.Pin_0, Part2.GND
  N2: Part1.A2, Part1.D10_PWM/SS, R1.Pin_0, R5.Pin_0, Part2.VCC
  N3: Part1.A3, J2.pin2
  N4: Part1.A4/SDA, R7.Pin_0, Part2.CS
  N5: Part1.A5/SCL, J3.pin2
  N6: Part1.D8, R7.Pin_1
  N7: Part1.D9_PWM, R8.Pin_1
  N8: Part1.D11_PWM/MOSI, Part2.MOSI
  N9: Part1.D12/MISO, J2.pin1
  N10: Part1.D2, R3.Pin_1
  N11: Part1.D3_PWM, R2.Pin_1
  N12: Part1.D4, R1.Pin_1
  N13: Part1.D5_PWM, R5.Pin_1
  N14: Part1.D6_PWM, R4.Pin_1
  N15: Part1.D7, R6.Pin_1
  N16: R2.Pin_0, Part2.MISO
  N17: R4.Pin_0, J3.pin1
  N18: R6.Pin_0, R8.Pin_0, Part2.SCK

notes:
  1
  8
  16
  9
  <==  Columns 1-8  ==>
  <==  Rows 4-8 ==>
  < Rows 1-3 >
  All resistors are 330 ohms. Display can be row anode or row cathode.

// code stored in the sketch: Blink.ino
/*=====================================================================
  This program is free software: you can redistribute it and/or modify
  it under the terms of the GNU General Public License as published by
  the Free Software Foundation, either version 3 of the License, or
  (at your option) any later version.

  This program is distributed in the hope that it will be useful,
  but WITHOUT ANY WARRANTY; without even the implied warranty of
  MERCHANTABILITY or FITNESS FOR A PARTICULAR PURPOSE.  See the
  GNU General Public License for more details.

  You should have received a copy of the GNU General Public License
  along with this program.  If not, see <http://www.gnu.org/licenses/>.
  ---------------------------------------------------------------------
  Purpose : Blink two LEDs alternatively.
  Date    : 21 Nov 2015
  Boards  : ArduinoUno, LaunchPadF5529
  =====================================================================
*/

// Comment/uncomment as suitable for your hardware
// #define LaunchPadF5529

#ifdef LaunchPadF5529
#define LED1 RED_LED // on-board, aka P1_0
#define LED2 GREEN_LED // on-board, aka P4_7
#else
#define LED1 13 // on-board
#define LED2 2 // external
#endif

void setup() {                
  pinMode(LED1, OUTPUT);
  pinMode(LED2, OUTPUT);
}

void loop() {
  digitalWrite(LED1, HIGH);
  digitalWrite(LED2, LOW);
  delay(1000);

  digitalWrite(LED1, LOW);
  digitalWrite(LED2, HIGH);
  delay(1000);
}

// code stored in the sketch: LedMatrix.ino
/*=====================================================================
  This program is free software: you can redistribute it and/or modify
  it under the terms of the GNU General Public License as published by
  the Free Software Foundation, either version 3 of the License, or
  (at your option) any later version.

  This program is distributed in the hope that it will be useful,
  but WITHOUT ANY WARRANTY; without even the implied warranty of
  MERCHANTABILITY or FITNESS FOR A PARTICULAR PURPOSE.  See the
  GNU General Public License for more details.

  You should have received a copy of the GNU General Public License
  along with this program.  If not, see <http://www.gnu.org/licenses/>.
  ---------------------------------------------------------------------
  Purpose : Drive an 8x8 LED matrix without any IC.
  Date    : 13 Dec 2015
  Boards  : ArduinoUno
  =====================================================================
*/

// Adapted from:
// Arduino Cookbook by Michael Margolis. 2011. Section 7.8

// Wiring connections from uC to display: (below are pin numbers on display):
// Columns on LED (left to right): 13, 3, 4, 10, 6, 11, 15, 16
// Rows on LED (top to bottom): 5, 2, 7, 1, 12, 8, 14, 9
const int columnPins[] = {2, 3, 4, 5, 6, 7, 8, 9};
const int rowPins[] = {19, 18, 17, 16, 15, 12, 11, 10};

#define ROW_CATHODE
#ifdef ROW_CATHODE
#define ROW_ON LOW
#define COL_ON HIGH
#else
#define ROW_ON HIGH
#define COL_ON LOW
#endif

byte bigHeart[] = {
  B01100110,
  B11111111,
  B11111111,
  B11111111,
  B01111110,
  B00111100,
  B00011000,
  B00000000
};

byte smallHeart[] = {
  B00000000,
  B00000000,
  B00010100,
  B00111110,
  B00111110,
  B00011100,
  B00001000,
  B00000000
};

void show( byte * image, unsigned long duration) {
  unsigned long start = millis();
  while (start + duration > millis()) {
    for (int row = 0; row < 8; row++) {
      digitalWrite(rowPins[row], ROW_ON);
      for (int column = 0; column < 8; column++) {
        boolean pixel = bitRead(image[row], column);
        if (pixel == 1) {
          digitalWrite(columnPins[column], COL_ON); // make the circuit
        }
        delayMicroseconds(300);
        digitalWrite(columnPins[column], !COL_ON);
      }
      digitalWrite(rowPins[row], !ROW_ON);
    }
  }
}

void setup() {
  for (int i = 0; i < 8; i++) {
    pinMode(rowPins[i], OUTPUT);
    pinMode(columnPins[i], OUTPUT);
    digitalWrite(columnPins[i], LOW);
  }
}

void loop() {
  show(smallHeart, 80);
  show(bigHeart, 160);
  delay(800);
}

// code stored in the sketch: sss.ino
/*=====================================================================
  This program is free software: you can redistribute it and/or modify
  it under the terms of the GNU General Public License as published by
  the Free Software Foundation, either version 3 of the License, or
  (at your option) any later version.

  This program is distributed in the hope that it will be useful,
  but WITHOUT ANY WARRANTY; without even the implied warranty of
  MERCHANTABILITY or FITNESS FOR A PARTICULAR PURPOSE.  See the
  GNU General Public License for more details.

  You should have received a copy of the GNU General Public License
  along with this program.  If not, see <http://www.gnu.org/licenses/>.
  ---------------------------------------------------------------------
  Purpose : Blink two LEDs alternatively.
  Date    : 21 Nov 2015
  Board   : ArduinoUno, LaunchPadF5529
  =====================================================================
*/

// Comment/uncomment as suitable to your hardware
// #define LaunchPadF5529

#ifdef LaunchPadF5529
#define LED1 RED_LED // on-board, aka P1_0
#define LED2 GREEN_LED // on-board, aka P4_7
#else
#define LED1 13 // on-board
#define LED2 2 // external
#endif

void setup() {                
  pinMode(LED1, OUTPUT);
  pinMode(LED2, OUTPUT);
}

void loop() {
  digitalWrite(LED1, HIGH);
  digitalWrite(LED2, LOW);
  delay(1000);

  digitalWrite(LED1, LOW);
  digitalWrite(LED2, HIGH);
  delay(1000);
}
