# Fritzing sketch PIR-MotionDetector (saved by Fritzing 0.9.2b)
breadboards: 1

parts:
  Part1 = Arduino Uno (Rev3)
  PIR1 = PIR sensor

nets:
  N1: Part1.D2, PIR1.SIG
  5V: Part1.5V, PIR1.VDD
  GND: Part1.GND, PIR1.GND

// code stored in the sketch: Blink.ino
/*=====================================================================
  This program is free software: you can redistribute it and/or modify
  it under the terms of the GNU General Public License as published by
  the Free Software Foundation, either version 3 of the License, or
  (at your option) any later version.

  This program is distributed in the hope that it will be useful,
  but WITHOUT ANY WARRANTY; without even the implied warranty of
  MERCHANTABILITY or FITNESS FOR A PARTICULAR PURPOSE.  See the
  GNU General Public License for more details.

  You should have received a copy of the GNU General Public License
  along with this program.  If not, see <http://www.gnu.org/licenses/>.
  ---------------------------------------------------------------------
  Purpose : Blink two LEDs alternatively.
  Date    : 21 Nov 2015
  Boards  : ArduinoUno, LaunchPadF5529
  =====================================================================
*/

// Comment/uncomment as suitable for your hardware
// #define LaunchPadF5529

#ifdef LaunchPadF5529
#define LED1 RED_LED // on-board, aka P1_0
#define LED2 GREEN_LED // on-board, aka P4_7
#else
#define LED1 13 // on-board
#define LED2 2 // external
#endif

void setup() {                
  pinMode(LED1, OUTPUT);
  pinMode(LED2, OUTPUT);
}

void loop() {
  digitalWrite(LED1, HIGH);
  digitalWrite(LED2, LOW);
  delay(1000);

  digitalWrite(LED1, LOW);
  digitalWrite(LED2, HIGH);
  delay(1000);
}

// code stored in the sketch: PIR-MotionDetector.ino
/*=====================================================================
  This program is free software: you can redistribute it and/or modify
  it under the terms of the GNU General Public License as published by
  the Free Software Foundation, either version 3 of the License, or
  (at your option) any later version.

  This program is distributed in the hope that it will be useful,
  but WITHOUT ANY WARRANTY; without even the implied warranty of
  MERCHANTABILITY or FITNESS FOR A PARTICULAR PURPOSE.  See the
  GNU General Public License for more details.

  You should have received a copy of the GNU General Public License
  along with this program.  If not, see <http://www.gnu.org/licenses/>.
  ---------------------------------------------------------------------
  Purpose : Using a PIR module we detect motion. Debouncing is used in
            such a way that current motion has to stop for a minimum
            time interval before we record a new motion.
  Date    : 22 Feb 2016
  Boards  : ArduinoUno, LaunchPadF5529
  =====================================================================
*/

// Source: Kristian Gohlke / krigoo@gmail.com / http://krx.at

// Comment/uncomment as suitable for your hardware
// #define LaunchPadF5529

#ifdef LaunchPadF5529
int pirPin = P2_0;
int ledPin = RED_LED;
#else
int pirPin = 3;
int ledPin = 13;
#endif

int calibrationTime = 30; // 10-60 secs in datasheet
long unsigned int motionStartTs; // timestamp of start of motion
long unsigned int pauseInterval = 5000; // idle time in ms to end current motion event
boolean lockLow = true;
boolean takeLowTime;  

void calibrate(int warmupTime)
{
  Serial.print("Calibrating sensor ");
  for(int i = 0; i < warmupTime; i++){
    Serial.print(".");
    delay(1000);
  }
  Serial.println(" done");
  Serial.println("SENSOR ACTIVE");
}

void setup()
{
  Serial.begin(9600);
  pinMode(pirPin, INPUT);
  digitalWrite(pirPin, LOW);

  pinMode(ledPin, OUTPUT);
  digitalWrite(ledPin, LOW);

  calibrate(calibrationTime);
  
  delay(50);
}

void loop()
{
     if(digitalRead(pirPin) == HIGH){
       digitalWrite(ledPin, HIGH);   //the led visualizes the sensors output pin state
       if(lockLow){  
         //makes sure we wait for a transition to LOW before any further output is made:
         lockLow = false;            
         Serial.println("---");
         Serial.print("motion detected at ");
         Serial.print(millis()/1000);
         Serial.println(" sec"); 
         delay(50);
         }         
         takeLowTime = true;
       }

     if(digitalRead(pirPin) == LOW){       
       digitalWrite(ledPin, LOW);  //the led visualizes the sensors output pin state

       if(takeLowTime){
        lowIn = millis();          //save the time of the transition from high to LOW
        takeLowTime = false;       //make sure this is only done at the start of a LOW phase
        }
       //if the sensor is low for more than the given pause, 
       //we assume that no more motion is going to happen
       if(!lockLow && millis() - lowIn > pause){  
           //makes sure this block of code is only executed again after 
           //a new motion sequence has been detected
           lockLow = true;                        
           Serial.print("motion ended at ");      //output
           Serial.print((millis() - pause)/1000);
           Serial.println(" sec");
           delay(50);
           }
       }
  }

// code stored in the sketch: sss.ino
/*=====================================================================
  This program is free software: you can redistribute it and/or modify
  it under the terms of the GNU General Public License as published by
  the Free Software Foundation, either version 3 of the License, or
  (at your option) any later version.

  This program is distributed in the hope that it will be useful,
  but WITHOUT ANY WARRANTY; without even the implied warranty of
  MERCHANTABILITY or FITNESS FOR A PARTICULAR PURPOSE.  See the
  GNU General Public License for more details.

  You should have received a copy of the GNU General Public License
  along with this program.  If not, see <http://www.gnu.org/licenses/>.
  ---------------------------------------------------------------------
  Purpose : Blink two LEDs alternatively.
  Date    : 21 Nov 2015
  Board   : ArduinoUno, LaunchPadF5529
  =====================================================================
*/

// Comment/uncomment as suitable to your hardware
// #define LaunchPadF5529

#ifdef LaunchPadF5529
#define LED1 RED_LED // on-board, aka P1_0
#define LED2 GREEN_LED // on-board, aka P4_7
#else
#define LED1 13 // on-board
#define LED2 2 // external
#endif

void setup() {                
  pinMode(LED1, OUTPUT);
  pinMode(LED2, OUTPUT);
}

void loop() {
  digitalWrite(LED1, HIGH);
  digitalWrite(LED2, LOW);
  delay(1000);

  digitalWrite(LED1, LOW);
  digitalWrite(LED2, HIGH);
  delay(1000);
}
