# Fritzing sketch RTC-IN1307 (saved by Fritzing 0.9.2b)
breadboards: 1

parts:
  S1 = Pushbutton [package="[THT]"]  # not connected
  S2 = Pushbutton [package="[THT]"]  # not connected
  S3 = Pushbutton [package="[THT]"]  # not connected
  S4 = Pushbutton [package="[THT]"]  # not connected
  J4 = male pin header, 2 pins [form="♂ (male)"]  # not connected
  J2 = double row male pin header, 10 pins [form="♂ (male)"]  # not connected
  J5 = double row male pin header, 10 pins [form="♂ (male)"]  # not connected
  J6 = double row male pin header, 10 pins [form="♂ (male)"]
  J7 = double row male pin header, 10 pins [form="♂ (male)"]
  J10 = male pin header, 3 pins [form="♂ (male)"]  # not connected
  J11 = male pin header, 3 pins [form="♂ (male)"]
  J8 = male pin header, 9 pins [form="♂ (male)"]
  J9 = male pin header, 9 pins [form="♂ (male)"]
  R1 = Resistor [tolerance=±5% resistance=10k package=THT]
  IC1 = DS1307 [package=THT]
  BAT1 = Battery Holders [package=battcom_20mm_pth]
  R2 = Resistor [tolerance=±5% resistance=10k package=THT]
  Y1 = CRYSTAL [package=crystal-32khz-smd_epson_mc146]

nets:
  N1: J6.pin1, R1.Pin_0, IC1.+V, R2.Pin_0
  N2: J7.pin9, R1.Pin_1, IC1.SCL_-_I2C_Clock
  N3: J7.pin10, IC1.SDA_-_I2C_Data, R2.Pin_1
  N4: J11.pin1, IC1.0V, BAT1.-
  N5: J8.pin1, J9.pin1
  N6: J8.pin2, J9.pin2
  N7: J8.pin3, J9.pin3
  N8: J8.pin4, J9.pin4
  N9: J8.pin7, J9.pin7
  N10: J8.pin8, J9.pin8
  N11: J8.pin9, J9.pin9
  N12: IC1.X1_-_Crystal, Y1.2
  N13: IC1.X2_-_Crystal, Y1.1
  N14: IC1.Vbat_-_Backup_Supply, BAT1.+

notes:
  GND
  LED
  P2.0
  P7.4
  P2.2
  RST
  P3.1
  P3.0
  P2.6
  P8.1
  P2.3
  P1.2
  P2.5
  P8.2
  P4.3
  P1.5
  P4.0
  P1.3
  P3.7
  P2.4
  P1.4
  P3.3
  P2.7
  P3.2
  P1.6
  P4.1
  P6.5
  P3.4
  P6.6
  3V3
  P4.2
  P3.5
  5V
  P6.3
  P6.4
  P6.0
  P7.0
  P6.2
  P3.6
  P6.1
  M430F5529
  RTS >>
  TXD >>
  RXD <<
  CTS <<
  TST
  BSL
  P2.1
  P1.1
  P1.0
  P4.7
  USB
  MSP-EXP430F5529LP
  IEDF
  You may need to try other values for the pullup resistors if RTC chip is not responding. DS1307 is shown but the pinout is same as IN1307. This chip requires 5V supply. Crystal is 32.768 kHz.

// code stored in the sketch: ReedSwitch.ino
/*=====================================================================
  This program is free software: you can redistribute it and/or modify
  it under the terms of the GNU General Public License as published by
  the Free Software Foundation, either version 3 of the License, or
  (at your option) any later version.

  This program is distributed in the hope that it will be useful,
  but WITHOUT ANY WARRANTY; without even the implied warranty of
  MERCHANTABILITY or FITNESS FOR A PARTICULAR PURPOSE.  See the
  GNU General Public License for more details.

  You should have received a copy of the GNU General Public License
  along with this program.  If not, see <http://www.gnu.org/licenses/>.
  ---------------------------------------------------------------------
  Purpose : Detect door open/close events using a reed switch.
						This example shows how to write interrupt code.
  Date    : 21 Nov 2015
  Boards  : ArduinoUno, LaunchPadF5529
  =====================================================================
*/

// Comment/uncomment as suitable for your hardware
// #define LaunchPadF5529

#ifdef LaunchPadF5529
int reedSwitch = P2_4; // pins of P1 and P2 are interrupt capable
#else
// Ref. https://www.arduino.cc/en/Reference/AttachInterrupt
int reedSwitch = 2; // pins 2 and 3 are interrupt capable on Uno
#endif

boolean prevDoorOpen = false;

// We use volatile because variables are changed within ISR.
// Compiler will not optimize volatile variables.
volatile boolean doorOpen = false;
volatile boolean stateChange = false;
volatile int interruptTs = 0;

void setup() {
  Serial.begin(115200);
  pinMode(reedSwitch, INPUT_PULLUP);

  #ifdef LaunchPadF5529
  attachInterrupt(reedSwitch, onDoorOpen, CHANGE);
  #else
  attachInterrupt(digitalPinToInterrupt(reedSwitch), onDoorOpen, CHANGE);
  #endif
}

void loop() {
  if (stateChange) {
    if (doorOpen) {
      Serial.println("\nSomeone has opened the door!");
    }
    else {
      Serial.println("\nSomeone has closed the door!");
    }
    stateChange = false;
  }
}

void onDoorOpen() {
  // software debouncing: 0 ms to bypass
  if ((long)(millis() - interruptTs) >= 0) {
    interruptTs = millis();

		// Note the state, print later.
    // Serial cannot be used here since further
    // interrupts are disabled within an ISR.
		// It is also good design to do minimal stuff
    // within ISR.
    stateChange = true;
    doorOpen = digitalRead(reedSwitch);
  }
}

// code stored in the sketch: RTC-IN1307.ino
/*=====================================================================
  This program is free software: you can redistribute it and/or modify
  it under the terms of the GNU General Public License as published by
  the Free Software Foundation, either version 3 of the License, or
  (at your option) any later version.

  This program is distributed in the hope that it will be useful,
  but WITHOUT ANY WARRANTY; without even the implied warranty of
  MERCHANTABILITY or FITNESS FOR A PARTICULAR PURPOSE.  See the
  GNU General Public License for more details.

  You should have received a copy of the GNU General Public License
  along with this program.  If not, see <http://www.gnu.org/licenses/>.
  ---------------------------------------------------------------------
  Purpose : Interface to Real-Time Clock (RTC) chip IN1307, which has
            an I2C interface. DS1307 is an equivalent chip but is not
            tested with this code. Code allows users to set the time
            via UART. RTClib is used in this code.
  Date    : 07 Jan 2016
  Boards  : ArduinoUno, LaunchPadF5529
  =====================================================================
*/

// RTClib:
// https://github.com/jcw/RTClib

// Comment/uncomment as suitable for your hardware
// #define LaunchPadF5529

#include <Wire.h>
#include <RTClib.h>

RTC_DS1307 RTC;

void printDateTime(DateTime inDt)
{
  Serial.print(inDt.day(), DEC);
  Serial.print('/');
  Serial.print(inDt.month(), DEC);
  Serial.print('/');
  Serial.print(inDt.year(), DEC);
  Serial.print(' ');
  Serial.print(inDt.hour(), DEC);
  Serial.print(':');
  Serial.print(inDt.minute(), DEC);
  Serial.print(':');
  Serial.print(inDt.second(), DEC);  
}

DateTime* readInputTime()
{
  // Default Energia distribution has SERIAL_BUFFER_SIZE set to 16
  // in hardware/msp430/cores/msp430/HardwareSerial.cpp
  // Change this to 64 so that at least 19 bytes can be stored in Serial buffer

  int dd, mm, yyyy, hh, ii, ss;

  // dd/mm/yyyy hh:ii:ss in 24-hour format
  // Use 24/03/2016 11:22:33, not 24/3/2016 11:22:33
  while (Serial.available()){
    dd = Serial.parseInt();
    mm = Serial.parseInt();
    yyyy = Serial.parseInt();
    hh = Serial.parseInt();
    ii = Serial.parseInt();
    ss = Serial.parseInt();
    DateTime *dt = new DateTime(yyyy, mm, dd, hh, ii, ss);
    return dt;
  }
  return NULL;
}

void setup()
{
  Serial.begin(9600);
  Serial.println(F("Initializing ..."));
  Wire.begin();
  RTC.begin();

  delay(100);
  while (!RTC.isrunning()) {
    Serial.println(F("RTC is NOT running. Clearing CH bit ..."));
    RTC.writeByteInRam(0, 0); // Clear CH bit
    delay(100);

    // For a start, set time based on when this code was compiled
    RTC.adjust(DateTime(__DATE__, __TIME__));
  }
  
  // Try out 12-hour format, assuming 5 PM
  // RTC.writeByteInRam(0x02, 0x65);
  // delay(10);
}

void loop()
{
  // Read time as user input via UART
  DateTime *startDt = readInputTime();
  if (startDt) RTC.adjust(*startDt);

  // Get current time and print it in regular intervals  
  DateTime currDt = RTC.now();
  printDateTime(currDt);
  Serial.println();
  delay(1000);
}
