# Fritzing sketch RgbLed-LaunchPadF5529 (saved by Fritzing 0.9.2b)
breadboards: 1

parts:
  S1 = Pushbutton [package="[THT]"]  # not connected
  S2 = Pushbutton [package="[THT]"]  # not connected
  S3 = Pushbutton [package="[THT]"]  # not connected
  S4 = Pushbutton [package="[THT]"]  # not connected
  J4 = male pin header, 2 pins [form="♂ (male)"]  # not connected
  J2 = double row male pin header, 10 pins [form="♂ (male)"]
  J5 = double row male pin header, 10 pins [form="♂ (male)"]  # not connected
  J6 = double row male pin header, 10 pins [form="♂ (male)"]  # not connected
  J7 = double row male pin header, 10 pins [form="♂ (male)"]  # not connected
  J10 = male pin header, 3 pins [form="♂ (male)"]  # not connected
  J11 = male pin header, 3 pins [form="♂ (male)"]
  J8 = male pin header, 9 pins [form="♂ (male)"]
  J9 = male pin header, 9 pins [form="♂ (male)"]
  R1 = Resistor [tolerance=±5% resistance=100 package=THT]
  R2 = Resistor [tolerance=±5% resistance=100 package=THT]
  R3 = Resistor [tolerance=±5% resistance=100 package=THT]
  LED1 = RGB LED - (4 legs) [package="5 mm [THT]"]

nets:
  N1: J2.pin1, R1.Pin_0
  N2: J2.pin2, R2.Pin_1
  N3: J2.pin3, R3.Pin_1
  N4: J11.pin3, LED1.green_cathode
  N5: J8.pin1, J9.pin1
  N6: J8.pin2, J9.pin2
  N7: J8.pin3, J9.pin3
  N8: J8.pin4, J9.pin4
  N9: J8.pin7, J9.pin7
  N10: J8.pin8, J9.pin8
  N11: J8.pin9, J9.pin9
  N12: R1.Pin_1, LED1.blue_cathode
  N13: R2.Pin_0, LED1.common_anode
  N14: R3.Pin_0, LED1.red_cathode

notes:
  GND
  LED
  P2.0
  P7.4
  P2.2
  RST
  P3.1
  P3.0
  P2.6
  P8.1
  P2.3
  P1.2
  P2.5
  P8.2
  P4.3
  P1.5
  P4.0
  P1.3
  P3.7
  P2.4
  P1.4
  P3.3
  P2.7
  P3.2
  P1.6
  P4.1
  P6.5
  P3.4
  P6.6
  3V3
  P4.2
  P3.5
  5V
  P6.3
  P6.4
  P6.0
  P7.0
  P6.2
  P3.6
  P6.1
  M430F5529
  RTS >>
  TXD >>
  RXD <<
  CTS <<
  TST
  BSL
  P2.1
  P1.1
  P1.0
  P4.7
  USB
  MSP-EXP430F5529LP
  IEDF
  All resistors are 100 ohms

// code stored in the sketch: RgbLed.ino
/*=====================================================================
  This program is free software: you can redistribute it and/or modify
  it under the terms of the GNU General Public License as published by
  the Free Software Foundation, either version 3 of the License, or
  (at your option) any later version.

  This program is distributed in the hope that it will be useful,
  but WITHOUT ANY WARRANTY; without even the implied warranty of
  MERCHANTABILITY or FITNESS FOR A PARTICULAR PURPOSE.  See the
  GNU General Public License for more details.

  You should have received a copy of the GNU General Public License
  along with this program.  If not, see <http://www.gnu.org/licenses/>.
  ---------------------------------------------------------------------
  Purpose : Change colours on an RGB LED.
  Date    : 21 Nov 2015
  Boards  : ArduinoUno, LaunchPadF5529
  =====================================================================
*/

// Comment/uncomment as suitable for your hardware
// #define LaunchPadF5529

#ifdef LaunchPadF5529
#define R_LED P2_5
#define G_LED P2_4
#define B_LED P1_5
#else
#define R_LED 2
#define G_LED 3
#define B_LED 4
#endif

void setup() {                
}

void loop() {
  // Use sin() to obtain smooth transitions
  // For abrupt transitions, try random(255)
  for (unsigned char i=0; i<256; i+=5) {
    analogWrite(R_LED, map(1000*sin(i*2*PI/255),-1000,1000,255,0));
    analogWrite(G_LED, map(1000*sin(2+i*2*PI/255),-1000,1000,255,0));
    analogWrite(B_LED, map(1000*sin(4+i*2*PI/255),-1000,1000,255,0));
    delay(10);
  }
}
