# Fritzing sketch ServoPushbutton (saved by Fritzing 0.9.2b)
breadboards: 1

parts:
  S1 = Pushbutton [package="[THT]"]  # not connected
  S2 = Pushbutton [package="[THT]"]  # not connected
  S3 = Pushbutton [package="[THT]"]  # not connected
  S4 = Pushbutton [package="[THT]"]  # not connected
  J4 = male pin header, 2 pins [form="♂ (male)"]  # not connected
  J2 = double row male pin header, 10 pins [form="♂ (male)"]
  J5 = double row male pin header, 10 pins [form="♂ (male)"]  # not connected
  J6 = double row male pin header, 10 pins [form="♂ (male)"]  # not connected
  J7 = double row male pin header, 10 pins [form="♂ (male)"]  # not connected
  J10 = male pin header, 3 pins [form="♂ (male)"]  # not connected
  J11 = male pin header, 3 pins [form="♂ (male)"]
  J8 = male pin header, 9 pins [form="♂ (male)"]
  J9 = male pin header, 9 pins [form="♂ (male)"]
  J12 = Basic Servo

nets:
  N1: J2.pin4, J12.pulse
  N2: J11.pin1, J12.gnd
  N3: J11.pin3, J12.vcc
  N4: J8.pin1, J9.pin1
  N5: J8.pin2, J9.pin2
  N6: J8.pin3, J9.pin3
  N7: J8.pin4, J9.pin4
  N8: J8.pin7, J9.pin7
  N9: J8.pin8, J9.pin8
  N10: J8.pin9, J9.pin9

notes:
  GND
  LED
  P2.0
  P7.4
  P2.2
  RST
  P3.1
  P3.0
  P2.6
  P8.1
  P2.3
  P1.2
  P2.5
  P8.2
  P4.3
  P1.5
  P4.0
  P1.3
  P3.7
  P2.4
  P1.4
  P3.3
  P2.7
  P3.2
  P1.6
  P4.1
  P6.5
  P3.4
  P6.6
  3V3
  P4.2
  P3.5
  5V
  P6.3
  P6.4
  P6.0
  P7.0
  P6.2
  P3.6
  P6.1
  M430F5529
  RTS >>
  TXD >>
  RXD <<
  CTS <<
  TST
  BSL
  P2.1
  P1.1
  P1.0
  P4.7
  USB
  MSP-EXP430F5529LP
  IEDF

// code stored in the sketch: ServoPushbutton.ino
/*=====================================================================
  This program is free software: you can redistribute it and/or modify
  it under the terms of the GNU General Public License as published by
  the Free Software Foundation, either version 3 of the License, or
  (at your option) any later version.

  This program is distributed in the hope that it will be useful,
  but WITHOUT ANY WARRANTY; without even the implied warranty of
  MERCHANTABILITY or FITNESS FOR A PARTICULAR PURPOSE.  See the
  GNU General Public License for more details.

  You should have received a copy of the GNU General Public License
  along with this program.  If not, see <http://www.gnu.org/licenses/>.
  ---------------------------------------------------------------------
  Purpose : Control servo movement using push buttons.
  Date    : 21 Nov 2015
  Boards  : ArduinoUno, LaunchPadF5529
  =====================================================================
*/

// Comment/uncomment as suitable for your hardware
// #define LaunchPadF5529

#ifdef LaunchPadF5529
#define PB1 PUSH1 // on-board, aka P2_1
#define PB2 PUSH2 // on-board, aka P1_1
#define CTRL P1_4
#else
#define PB1 2 // external
#define PB2 3 // external
#define CTRL 9
#endif

#include <Servo.h>
 
Servo myservo; // a maximum of eight servo objects can be created

int pos = 0;
 
void setup()
{
  myservo.attach(CTRL);
  pinMode(PB1, INPUT_PULLUP);
  pinMode(PB2, INPUT_PULLUP);

  #ifdef LaunchPadF5529
  pinMode(RED_LED, OUTPUT);
  pinMode(GREEN_LED, OUTPUT);
  #endif

  sweep(); // test the full range once
}
 
 
void loop()
{
  pushbuttons();
}

void pushbuttons()
{
  if (!digitalRead(PB1)) {
    pos -= 5;
    delay(15);

    #ifdef LaunchPadF5529
    digitalWrite(RED_LED, HIGH);
    delay(100);
    digitalWrite(RED_LED, LOW);
    #endif
  }
  else if (!digitalRead(PB2)) {
    pos += 5;
    delay(15);

    #ifdef LaunchPadF5529
    digitalWrite(GREEN_LED, HIGH);
    delay(100);
    digitalWrite(GREEN_LED, LOW);
    #endif
  }

  if (pos>179) pos = 179;
  else if (pos<0) pos = 0;
  myservo.write(pos);
}

void sweep()
{
  for (pos = 0; pos < 180; pos += 1) {
    myservo.write(pos);
    delay(15);
  }
  for (pos = 180; pos>=1; pos -= 1) {                                
    myservo.write(pos);
    delay(15);
  }
}
