# Fritzing sketch Tetris-FC16 (saved by Fritzing 0.9.3b)
breadboards: 1

parts:
  Part1 = Arduino Uno (Rev3)
  Disp1 = LBT2088AH [part_number=LBT2088AH]  # not connected
  J3 = rounded female pin header, 5 pins [form="♀ (female rounded)"]
  S1 = Momentary Switch [package=ksa_sealed_tac_switch]
  S2 = Momentary Switch [package=ksa_sealed_tac_switch]
  S3 = Momentary Switch [package=ksa_sealed_tac_switch]
  S4 = Momentary Switch [package=ksa_sealed_tac_switch]
  D1 = Diode [package=diode-1n4148]
  D2 = Diode [package=diode-1n4148]
  D4 = Diode [package=diode-1n4148]
  R1 = Resistor [tolerance=±5% resistance=4.7k package="0805 [SMD]"]
  R2 = Resistor [tolerance=±5% resistance=4.7k package="0805 [SMD]"]
  R3 = Resistor [tolerance=±5% resistance=4.7k package="0805 [SMD]"]
  R4 = Resistor [tolerance=±5% resistance=4.7k package="0805 [SMD]"]
  R5 = Resistor [tolerance=±5% resistance=4.7k package="0805 [SMD]"]
  D5 = Diode [package=diode-1n4148]

nets:
  N1: Part1.D10_PWM/SS, J3.pin2
  N2: Part1.D11_PWM/MOSI, J3.pin3
  N3: Part1.D13/SCK, J3.pin1
  N4: Part1.D2, D1.C, D2.C, D4.C, R1.Pin_0, D5.C
  N5: Part1.D3_PWM, S1.1
  N6: Part1.D4, S3.1, D2.A
  N7: Part1.D5_PWM, S4.1, S4.2, R4.Pin_0
  N8: Part1.D6_PWM, S2.1, S2.2, R5.Pin_0
  N9: Part1.5V, S1.3, S2.3, S2.4, S3.3, S4.3, S4.4
  N10: Part1.GND, R1.Pin_1, R2.Pin_1, R3.Pin_1, R4.Pin_1, R5.Pin_1
  N11: S1.2, R2.Pin_0
  N12: S3.2, R3.Pin_0

notes:
  Pushbuttons trigger interrupts on pin 2 on the rising edge. To multiplex four of them, we use four diodes. Resistors are 4.7kΩ each.
  We show only one 8x8 display. This project uses the MAX7219 FC16 module containing four 8x8 display with driver control circuitry. The five pins of this module are shown.
  CS
  GND
  INT1
  VCC
  INT2
  SDO
  SDA
  SCL
  DIN
  CLK
  5V
  Any 5V DC source

// code stored in the sketch: Blink.ino
/*=====================================================================
  This program is free software: you can redistribute it and/or modify
  it under the terms of the GNU General Public License as published by
  the Free Software Foundation, either version 3 of the License, or
  (at your option) any later version.

  This program is distributed in the hope that it will be useful,
  but WITHOUT ANY WARRANTY; without even the implied warranty of
  MERCHANTABILITY or FITNESS FOR A PARTICULAR PURPOSE.  See the
  GNU General Public License for more details.

  You should have received a copy of the GNU General Public License
  along with this program.  If not, see <http://www.gnu.org/licenses/>.
  ---------------------------------------------------------------------
  Purpose : Blink two LEDs alternatively.
  Date    : 21 Nov 2015
  Boards  : ArduinoUno, LaunchPadF5529
  =====================================================================
*/

// Comment/uncomment as suitable for your hardware
// #define LaunchPadF5529

#ifdef LaunchPadF5529
#define LED1 RED_LED // on-board, aka P1_0
#define LED2 GREEN_LED // on-board, aka P4_7
#else
#define LED1 13 // on-board
#define LED2 2 // external
#endif

void setup() {                
  pinMode(LED1, OUTPUT);
  pinMode(LED2, OUTPUT);
}

void loop() {
  digitalWrite(LED1, HIGH);
  digitalWrite(LED2, LOW);
  delay(1000);

  digitalWrite(LED1, LOW);
  digitalWrite(LED2, HIGH);
  delay(1000);
}

// code stored in the sketch: sss.ino
/*=====================================================================
  This program is free software: you can redistribute it and/or modify
  it under the terms of the GNU General Public License as published by
  the Free Software Foundation, either version 3 of the License, or
  (at your option) any later version.

  This program is distributed in the hope that it will be useful,
  but WITHOUT ANY WARRANTY; without even the implied warranty of
  MERCHANTABILITY or FITNESS FOR A PARTICULAR PURPOSE.  See the
  GNU General Public License for more details.

  You should have received a copy of the GNU General Public License
  along with this program.  If not, see <http://www.gnu.org/licenses/>.
  ---------------------------------------------------------------------
  Purpose : Blink two LEDs alternatively.
  Date    : 21 Nov 2015
  Board   : ArduinoUno, LaunchPadF5529
  =====================================================================
*/

// Comment/uncomment as suitable to your hardware
// #define LaunchPadF5529

#ifdef LaunchPadF5529
#define LED1 RED_LED // on-board, aka P1_0
#define LED2 GREEN_LED // on-board, aka P4_7
#else
#define LED1 13 // on-board
#define LED2 2 // external
#endif

void setup() {                
  pinMode(LED1, OUTPUT);
  pinMode(LED2, OUTPUT);
}

void loop() {
  digitalWrite(LED1, HIGH);
  digitalWrite(LED2, LOW);
  delay(1000);

  digitalWrite(LED1, LOW);
  digitalWrite(LED2, HIGH);
  delay(1000);
}
