# Fritzing sketch Blynk-LM35 (saved by Fritzing 0.9.2b)
breadboards: 1

parts:
  U1 = NodeMCU V1.0
  T1 = LM35 Temperature Sensor [package="TO92 [THT]"]

nets:
  N1: U1.3V3, T1.+Vs
  GND: U1.GND, T1.GND
  N2: U1.A0, T1.Vout

notes:
  ==> To Power Supply / Laptop

custom parts:
  NodeMCU V1.0: ESP9266 based NodeMCU

// code stored in the sketch: Blink.ino
/*=====================================================================
  This program is free software: you can redistribute it and/or modify
  it under the terms of the GNU General Public License as published by
  the Free Software Foundation, either version 3 of the License, or
  (at your option) any later version.

  This program is distributed in the hope that it will be useful,
  but WITHOUT ANY WARRANTY; without even the implied warranty of
  MERCHANTABILITY or FITNESS FOR A PARTICULAR PURPOSE.  See the
  GNU General Public License for more details.

  You should have received a copy of the GNU General Public License
  along with this program.  If not, see <http://www.gnu.org/licenses/>.
  ---------------------------------------------------------------------
  Purpose : Blink two LEDs alternatively.
  Date    : 21 Nov 2015
  Boards  : ArduinoUno, LaunchPadF5529
  =====================================================================
*/

// Comment/uncomment as suitable for your hardware
// #define LaunchPadF5529

#ifdef LaunchPadF5529
#define LED1 RED_LED // on-board, aka P1_0
#define LED2 GREEN_LED // on-board, aka P4_7
#else
#define LED1 13 // on-board
#define LED2 2 // external
#endif

void setup() {                
  pinMode(LED1, OUTPUT);
  pinMode(LED2, OUTPUT);
}

void loop() {
  digitalWrite(LED1, HIGH);
  digitalWrite(LED2, LOW);
  delay(1000);

  digitalWrite(LED1, LOW);
  digitalWrite(LED2, HIGH);
  delay(1000);
}

// code stored in the sketch: Blynk-Blink.ino
/*=====================================================================
  This program is free software: you can redistribute it and/or modify
  it under the terms of the GNU General Public License as published by
  the Free Software Foundation, either version 3 of the License, or
  (at your option) any later version.

  This program is distributed in the hope that it will be useful,
  but WITHOUT ANY WARRANTY; without even the implied warranty of
  MERCHANTABILITY or FITNESS FOR A PARTICULAR PURPOSE.  See the
  GNU General Public License for more details.

  You should have received a copy of the GNU General Public License
  along with this program.  If not, see <http://www.gnu.org/licenses/>.
  ---------------------------------------------------------------------
  Purpose : Control an LED manually from the Blynk app. Update the
            code with your token, Wi-Fi SSID and password.
  Date    : 25 Jan 2016
  Boards  : NodeMCU
  =====================================================================
*/

#define BLYNK_PRINT Serial    // Comment out to disable prints

#include <ESP8266WiFi.h>
#include <BlynkSimpleEsp8266.h>

// Get Auth Token in the Blynk App.
char auth[] = "77a4294379494b1dac57297eb6d2e5c5";

void setup()
{
  Serial.begin(9600);
  Blynk.begin(auth, "andronicus", "rhjUk87uibio09");
}

void loop()
{
  Blynk.run();
}

// code stored in the sketch: Blynk-LM35.ino
/*=====================================================================
  This program is free software: you can redistribute it and/or modify
  it under the terms of the GNU General Public License as published by
  the Free Software Foundation, either version 3 of the License, or
  (at your option) any later version.

  This program is distributed in the hope that it will be useful,
  but WITHOUT ANY WARRANTY; without even the implied warranty of
  MERCHANTABILITY or FITNESS FOR A PARTICULAR PURPOSE.  See the
  GNU General Public License for more details.

  You should have received a copy of the GNU General Public License
  along with this program.  If not, see <http://www.gnu.org/licenses/>.
  ---------------------------------------------------------------------
  Purpose : Send temperature readings from LM35 and display the same
            on the Blynk app.
  Date    : 14 Mar 2016
  Boards  : NodeMCU
  =====================================================================
*/

// Blynk:
// https://github.com/blynkkk/blynk-library/releases
// http://www.blynk.cc/

#define BLYNK_PRINT Serial    // Comment this out to disable prints

#include <ESP8266WiFi.h>
#include <BlynkSimpleEsp8266.h>
#include <SimpleTimer.h>

char auth[] = "77a4294379494b1dac57297eb6d2e5c5";

int adcPin = 17;
float temperature;
SimpleTimer timer;

void setup()
{
  Serial.begin(9600);
  Blynk.begin(auth, "andronicus", "rhjUk87uibio09");

  // Timer-based callback
  timer.setInterval(1000L, sendReadings);
}

void sendReadings()
{
  Blynk.virtualWrite(10, temperature); // virtual pin 10
}

void loop()
{
  Blynk.run();
  timer.run();
  
  unsigned int adcValue = analogRead(adcPin);
  temperature = adcValue * 330 / 1024; // 3.3 VREF, 10-bit ADC, 10mV = 1 degree Celsius

  // Just for debugging
  Serial.print("ADC value: ");
  Serial.print(adcValue);
  Serial.print("; Current temperature (Celsius): ");
  Serial.println(temperature);
}

// code stored in the sketch: sss.ino
/*=====================================================================
  This program is free software: you can redistribute it and/or modify
  it under the terms of the GNU General Public License as published by
  the Free Software Foundation, either version 3 of the License, or
  (at your option) any later version.

  This program is distributed in the hope that it will be useful,
  but WITHOUT ANY WARRANTY; without even the implied warranty of
  MERCHANTABILITY or FITNESS FOR A PARTICULAR PURPOSE.  See the
  GNU General Public License for more details.

  You should have received a copy of the GNU General Public License
  along with this program.  If not, see <http://www.gnu.org/licenses/>.
  ---------------------------------------------------------------------
  Purpose : Blink two LEDs alternatively.
  Date    : 21 Nov 2015
  Board   : ArduinoUno, LaunchPadF5529
  =====================================================================
*/

// Comment/uncomment as suitable to your hardware
// #define LaunchPadF5529

#ifdef LaunchPadF5529
#define LED1 RED_LED // on-board, aka P1_0
#define LED2 GREEN_LED // on-board, aka P4_7
#else
#define LED1 13 // on-board
#define LED2 2 // external
#endif

void setup() {                
  pinMode(LED1, OUTPUT);
  pinMode(LED2, OUTPUT);
}

void loop() {
  digitalWrite(LED1, HIGH);
  digitalWrite(LED2, LOW);
  delay(1000);

  digitalWrite(LED1, LOW);
  digitalWrite(LED2, HIGH);
  delay(1000);
}
