# Fritzing sketch Blynk-RgbLed (saved by Fritzing 0.9.2b)
breadboards: 1

parts:
  U1 = NodeMCU V1.0
  LED1 = RGB LED - (4 legs) [package="5 mm [THT]"]
  R1 = Resistor [tolerance=±5% resistance=100 package=THT]

nets:
  N1: U1.3V3, R1.Pin_1
  N2: U1.D5, LED1.red_cathode
  N3: U1.D6, LED1.green_cathode
  N4: U1.D7, LED1.blue_cathode
  N5: LED1.common_anode, R1.Pin_0

notes:
  ==> To      Power Supply / Laptop
  This RGB LED is of the common anode type. Use a resistor per colour component for better control.

custom parts:
  NodeMCU V1.0: ESP9266 based NodeMCU

// code stored in the sketch: Blink.ino
/*=====================================================================
  This program is free software: you can redistribute it and/or modify
  it under the terms of the GNU General Public License as published by
  the Free Software Foundation, either version 3 of the License, or
  (at your option) any later version.

  This program is distributed in the hope that it will be useful,
  but WITHOUT ANY WARRANTY; without even the implied warranty of
  MERCHANTABILITY or FITNESS FOR A PARTICULAR PURPOSE.  See the
  GNU General Public License for more details.

  You should have received a copy of the GNU General Public License
  along with this program.  If not, see <http://www.gnu.org/licenses/>.
  ---------------------------------------------------------------------
  Purpose : Blink two LEDs alternatively.
  Date    : 21 Nov 2015
  Boards  : ArduinoUno, LaunchPadF5529
  =====================================================================
*/

// Comment/uncomment as suitable for your hardware
// #define LaunchPadF5529

#ifdef LaunchPadF5529
#define LED1 RED_LED // on-board, aka P1_0
#define LED2 GREEN_LED // on-board, aka P4_7
#else
#define LED1 13 // on-board
#define LED2 2 // external
#endif

void setup() {                
  pinMode(LED1, OUTPUT);
  pinMode(LED2, OUTPUT);
}

void loop() {
  digitalWrite(LED1, HIGH);
  digitalWrite(LED2, LOW);
  delay(1000);

  digitalWrite(LED1, LOW);
  digitalWrite(LED2, HIGH);
  delay(1000);
}

// code stored in the sketch: Blynk-Blink.ino
/*=====================================================================
  This program is free software: you can redistribute it and/or modify
  it under the terms of the GNU General Public License as published by
  the Free Software Foundation, either version 3 of the License, or
  (at your option) any later version.

  This program is distributed in the hope that it will be useful,
  but WITHOUT ANY WARRANTY; without even the implied warranty of
  MERCHANTABILITY or FITNESS FOR A PARTICULAR PURPOSE.  See the
  GNU General Public License for more details.

  You should have received a copy of the GNU General Public License
  along with this program.  If not, see <http://www.gnu.org/licenses/>.
  ---------------------------------------------------------------------
  Purpose : Control an LED manually from the Blynk app. Update the
            code with your token, Wi-Fi SSID and password.
  Date    : 25 Jan 2016
  Boards  : NodeMCU
  =====================================================================
*/

#define BLYNK_PRINT Serial    // Comment out to disable prints

#include <ESP8266WiFi.h>
#include <BlynkSimpleEsp8266.h>

// Get Auth Token in the Blynk App.
char auth[] = "77a4294379494b1dac57297eb6d2e5c5";

void setup()
{
  Serial.begin(9600);
  Blynk.begin(auth, "andronicus", "rhjUk87uibio09");
}

void loop()
{
  Blynk.run();
}

// code stored in the sketch: Blynk-RgbLed.ino
/*=====================================================================
  This program is free software: you can redistribute it and/or modify
  it under the terms of the GNU General Public License as published by
  the Free Software Foundation, either version 3 of the License, or
  (at your option) any later version.

  This program is distributed in the hope that it will be useful,
  but WITHOUT ANY WARRANTY; without even the implied warranty of
  MERCHANTABILITY or FITNESS FOR A PARTICULAR PURPOSE.  See the
  GNU General Public License for more details.

  You should have received a copy of the GNU General Public License
  along with this program.  If not, see <http://www.gnu.org/licenses/>.
  ---------------------------------------------------------------------
  Purpose : Control an LED manually from the Blynk app. This code can
            be compiled and uploaded from Arduino IDE. Update the code
            with your token, Wi-Fi SSID and password.
  Date    : 25 Jan 2016
  Boards  : NodeMCU
  =====================================================================
*/

// Blynk:
// https://github.com/blynkkk/blynk-library/releases
// http://www.blynk.cc/

#define BLYNK_PRINT Serial    // Comment out to disable prints

#include <ESP8266WiFi.h>
#include <BlynkSimpleEsp8266.h>

// Get Auth Token in the Blynk App.
char auth[] = "xxx";

void setup()
{
  Serial.begin(9600);
  Blynk.begin(auth, "xxx", "xxx");
}

void loop()
{
  Blynk.run();
}

// code stored in the sketch: sss.ino
/*=====================================================================
  This program is free software: you can redistribute it and/or modify
  it under the terms of the GNU General Public License as published by
  the Free Software Foundation, either version 3 of the License, or
  (at your option) any later version.

  This program is distributed in the hope that it will be useful,
  but WITHOUT ANY WARRANTY; without even the implied warranty of
  MERCHANTABILITY or FITNESS FOR A PARTICULAR PURPOSE.  See the
  GNU General Public License for more details.

  You should have received a copy of the GNU General Public License
  along with this program.  If not, see <http://www.gnu.org/licenses/>.
  ---------------------------------------------------------------------
  Purpose : Blink two LEDs alternatively.
  Date    : 21 Nov 2015
  Board   : ArduinoUno, LaunchPadF5529
  =====================================================================
*/

// Comment/uncomment as suitable to your hardware
// #define LaunchPadF5529

#ifdef LaunchPadF5529
#define LED1 RED_LED // on-board, aka P1_0
#define LED2 GREEN_LED // on-board, aka P4_7
#else
#define LED1 13 // on-board
#define LED2 2 // external
#endif

void setup() {                
  pinMode(LED1, OUTPUT);
  pinMode(LED2, OUTPUT);
}

void loop() {
  digitalWrite(LED1, HIGH);
  digitalWrite(LED2, LOW);
  delay(1000);

  digitalWrite(LED1, LOW);
  digitalWrite(LED2, HIGH);
  delay(1000);
}
